// Logisim project 74xx.circ as structural Verilog: 33 circuits, main circuit README
module README (
);


  // Notes on the sheet:
  //   Logisim 74xx series integrated circuits library
  //   Copyright (C) 2015 by Stefan Rothe
  //   This library is licenced under the GNU General Public Licence version 3.
endmodule

// 7400
module DIP_7400 (
  input  A1,
  input  B1,
  input  A2,
  input  B2,
  input  A3,
  input  B3,
  input  A4,
  input  B4,
  output Q1,
  output Q2,
  output Q3,
  output Q4
);

  nand nand_1 (Q1, A1, B1);
  nand nand_2 (Q2, A2, B2);
  nand nand_3 (Q3, A3, B3);
  nand nand_4 (Q4, A4, B4);
endmodule

// 7402
module DIP_7402 (
  input  A1,
  input  B1,
  input  A2,
  input  B2,
  input  A3,
  input  B3,
  input  A4,
  input  B4,
  output Q1,
  output Q2,
  output Q3,
  output Q4
);

  nor nor_1 (Q1, A1, B1);
  nor nor_2 (Q2, A2, B2);
  nor nor_3 (Q3, A3, B3);
  nor nor_4 (Q4, A4, B4);
endmodule

// 7404
module DIP_7404 (
  input  A1,
  input  A2,
  input  A3,
  input  A4,
  input  A5,
  input  A6,
  output Q1,
  output Q2,
  output Q3,
  output Q4,
  output Q5,
  output Q6
);

  not not_1 (Q1, A1);
  not not_2 (Q2, A2);
  not not_3 (Q3, A3);
  not not_4 (Q4, A4);
  not not_5 (Q5, A5);
  not not_6 (Q6, A6);
endmodule

// 7408
module DIP_7408 (
  input  A1,
  input  B1,
  input  A2,
  input  B2,
  input  A3,
  input  B3,
  input  A4,
  input  B4,
  output Q1,
  output Q2,
  output Q3,
  output Q4
);

  and and_1 (Q1, A1, B1);
  and and_2 (Q2, A2, B2);
  and and_3 (Q3, A3, B3);
  and and_4 (Q4, A4, B4);
endmodule

// 7410
module DIP_7410 (
  input  A1,
  input  B1,
  input  C1,
  input  A2,
  input  B2,
  input  C2,
  input  A3,
  input  B3,
  input  C3,
  output Q1,
  output Q2,
  output Q3
);

  nand nand_1 (Q1, A1, B1, C1);
  nand nand_2 (Q2, A2, B2, C2);
  nand nand_3 (Q3, A3, B3, C3);
endmodule

// 7411
module DIP_7411 (
  input  A1,
  input  B1,
  input  C1,
  input  A2,
  input  B2,
  input  C2,
  input  A3,
  input  B3,
  input  C3,
  output Q1,
  output Q2,
  output Q3
);

  and and_1 (Q1, A1, B1, C1);
  and and_2 (Q2, A2, B2, C2);
  and and_3 (Q3, A3, B3, C3);
endmodule

// 7420
module DIP_7420 (
  input  A1,
  input  B1,
  input  C1,
  input  D1,
  input  A2,
  input  B2,
  input  C2,
  input  D2,
  output Q1,
  output Q2
);

  nand nand_1 (Q1, A1, B1, C1, D1);
  nand nand_2 (Q2, A2, B2, C2, D2);
endmodule

// 7421
module DIP_7421 (
  input  A1,
  input  B1,
  input  C1,
  input  D1,
  input  A2,
  input  B2,
  input  C2,
  input  D2,
  output Q1,
  output Q2
);

  and and_1 (Q1, A1, B1, C1, D1);
  and and_2 (Q2, A2, B2, C2, D2);
endmodule

// 7425
module DIP_7425 (
  input  A1,
  input  B1,
  input  C1,
  input  D1,
  input  A2,
  input  B2,
  input  C2,
  input  D2,
  output Q1,
  output Q2
);

  nor nor_1 (Q1, A1, B1, C1, D1);
  nor nor_2 (Q2, A2, B2, C2, D2);
endmodule

// 7427
module DIP_7427 (
  input  A1,
  input  B1,
  input  C1,
  input  A2,
  input  B2,
  input  C2,
  input  A3,
  input  B3,
  input  C3,
  output Q1,
  output Q2,
  output Q3
);

  nor nor_1 (Q1, A1, B1, C1);
  nor nor_2 (Q2, A2, B2, C2);
  nor nor_3 (Q3, A3, B3, C3);
endmodule

// 7432
module DIP_7432 (
  input  A1,
  input  B1,
  input  A2,
  input  B2,
  input  A3,
  input  B3,
  input  A4,
  input  B4,
  output Q1,
  output Q2,
  output Q3,
  output Q4
);

  or or_1 (Q1, A1, B1);
  or or_2 (Q2, A2, B2);
  or or_3 (Q3, A3, B3);
  or or_4 (Q4, A4, B4);
endmodule

// 7442
module DIP_7442 (
  input  D1,
  input  D2,
  input  D3,
  input  D4,
  output Q1,
  output Q2,
  output Q3,
  output Q4,
  output Q5,
  output Q6,
  output Q7,
  output Q8,
  output Q9,
  output Q10
);

  wire nand_1_out, nand_2_out, nand_3_out, nand_4_out, nand_5_out, nand_6_out, nand_7_out, not_1_out,
       not_2_out, not_3_out, not_4_out, not_5_out, not_6_out, not_7_out, not_8_out;

  not not_1 (not_1_out, D1);
  not not_2 (not_2_out, D2);
  not not_3 (not_3_out, D3);
  not not_4 (not_4_out, D4);
  not not_5 (not_5_out, not_1_out);
  not not_6 (not_6_out, not_2_out);
  not not_7 (not_7_out, not_3_out);
  not not_8 (not_8_out, not_4_out);
  nand nand_1 (nand_1_out, not_1_out, not_2_out);
  nand nand_2 (nand_2_out, not_5_out, not_2_out);
  nand nand_3 (nand_3_out, not_1_out, not_6_out);
  nand nand_4 (nand_4_out, not_5_out, not_6_out);
  nand nand_5 (nand_5_out, not_3_out, not_4_out);
  nand nand_6 (nand_6_out, not_7_out, not_4_out);
  nand nand_7 (nand_7_out, not_3_out, not_8_out);
  nand nand_8 (Q1, ~nand_1_out, ~nand_5_out);  // NAND_Gate
  nand nand_9 (Q2, ~nand_2_out, ~nand_5_out);  // NAND_Gate
  nand nand_10 (Q3, ~nand_3_out, ~nand_5_out);  // NAND_Gate
  nand nand_11 (Q4, ~nand_4_out, ~nand_5_out);  // NAND_Gate
  nand nand_12 (Q5, ~nand_1_out, ~nand_6_out);  // NAND_Gate
  nand nand_13 (Q6, ~nand_2_out, ~nand_6_out);  // NAND_Gate
  nand nand_14 (Q7, ~nand_3_out, ~nand_6_out);  // NAND_Gate
  nand nand_15 (Q8, ~nand_4_out, ~nand_6_out);  // NAND_Gate
  nand nand_16 (Q9, ~nand_1_out, ~nand_7_out);  // NAND_Gate
  nand nand_17 (Q10, ~nand_2_out, ~nand_7_out);  // NAND_Gate
endmodule

// 7451
module DIP_7451 (
  input  A1,
  input  B1,
  input  C1,
  input  D1,
  input  E1,
  input  F1,
  input  A2,
  input  B2,
  input  C2,
  input  D2,
  output Q1,
  output Q2
);

  wire and_1_out, and_2_out, and_3_out, and_4_out;

  and and_1 (and_1_out, A1, B1, C1);
  and and_2 (and_2_out, D1, E1, F1);
  and and_3 (and_3_out, A2, B2);
  and and_4 (and_4_out, C2, D2);
  nor nor_1 (Q1, and_1_out, and_2_out);
  nor nor_2 (Q2, and_3_out, and_4_out);
endmodule

// 7474
module DIP_7474 (
  input  SET1_,
  input  D1,
  input  CLK1,
  input  CLR1_,
  input  SET2_,
  input  D2,
  input  CLK2,
  input  CLR2_,
  output Q1,
  output Q1_,
  output Q2,
  output Q2_
);

  wire nand_1_out, nand_2_out, nand_3_out, nand_4_out, nand_5_out, nand_6_out, nand_7_out, nand_8_out,
       nand_9_out, nand_10_out, nand_11_out, nand_12_out, not_1_out, not_2_out, not_3_out, not_4_out;

  not not_1 (not_1_out, D1);
  not not_2 (not_2_out, D2);
  nand nand_1 (nand_1_out, SET1_, nand_2_out, nand_3_out);
  nand nand_2 (nand_2_out, D1, CLK1);
  nand nand_3 (nand_3_out, nand_1_out, nand_4_out, CLR1_);
  nand nand_4 (nand_4_out, CLK1, not_1_out);
  not not_3 (not_3_out, CLK1);
  nand nand_5 (nand_5_out, D2, CLK2);
  nand nand_6 (nand_6_out, SET2_, nand_5_out, nand_7_out);
  nand nand_7 (nand_7_out, nand_6_out, nand_8_out, CLR2_);
  nand nand_8 (nand_8_out, CLK2, not_2_out);
  not not_4 (not_4_out, CLK2);
  nand nand_9 (nand_9_out, nand_1_out, not_3_out);
  nand nand_10 (nand_10_out, not_3_out, nand_3_out);
  nand nand_11 (nand_11_out, nand_6_out, not_4_out);
  nand nand_12 (nand_12_out, not_4_out, nand_7_out);
  nand nand_13 (Q1, SET1_, nand_9_out, Q1_);
  nand nand_14 (Q1_, Q1, nand_10_out, CLR1_);
  nand nand_15 (Q2, SET2_, nand_11_out, Q2_);
  nand nand_16 (Q2_, Q2, nand_12_out, CLR2_);
endmodule

// 7476
module DIP_7476 (
  input  SET1_,
  input  J1,
  input  CLK1,
  input  K1,
  input  CLR1_,
  input  SET2_,
  input  J2,
  input  CLK2,
  input  K2,
  input  CLR2_,
  output Q1,
  output Q1_,
  output Q2,
  output Q2_
);

  wire not_1_out, not_2_out, not_3_out, not_4_out, not_5_out, not_6_out;

  not not_1 (not_1_out, SET1_);
  not not_2 (not_2_out, CLK1);
  not not_3 (not_3_out, CLR1_);
  not not_4 (not_4_out, SET2_);
  not not_5 (not_5_out, CLK2);
  not not_6 (not_6_out, CLR2_);
  J_K_Flip_Flop j_k_ff_1 (
    .J(J1), .clk(not_2_out), .K(K1), .Q(Q1), .Qn(Q1_), .preset(not_1_out), .reset(not_3_out));  // open: en
  J_K_Flip_Flop j_k_ff_2 (
    .J(J2), .clk(not_5_out), .K(K2), .Q(Q2), .Qn(Q2_), .preset(not_4_out), .reset(not_6_out));  // open: en
endmodule

// 7486
module DIP_7486 (
  input  A1,
  input  B1,
  input  A2,
  input  B2,
  input  A3,
  input  B3,
  input  A4,
  input  B4,
  output Q1,
  output Q2,
  output Q3,
  output Q4
);

  xor xor_1 (Q1, A1, B1);
  xor xor_2 (Q2, A2, B2);
  xor xor_3 (Q3, A3, B3);
  xor xor_4 (Q4, A4, B4);
endmodule

// 74147
module DIP_74147 (
  input  D1,
  input  D2,
  input  D3,
  input  D4,
  input  D5,
  input  D6,
  input  D7,
  input  D8,
  input  D9,
  output Q1,
  output Q2,
  output Q3,
  output Q4
);

  wire and_1_out, and_2_out, and_3_out, and_4_out, and_5_out, and_6_out, and_7_out, and_8_out, and_9_out,
       and_10_out, and_11_out, and_12_out, buffer_1_out, nor_1_out, not_1_out, not_2_out, not_3_out,
       not_4_out, not_5_out, not_6_out, not_7_out, not_8_out, not_9_out, not_10_out, not_11_out, not_12_out,
       not_13_out;

  not not_1 (not_1_out, D1);
  not not_2 (not_2_out, D2);
  not not_3 (not_3_out, D3);
  not not_4 (not_4_out, D4);
  not not_5 (not_5_out, D5);
  not not_6 (not_6_out, D6);
  not not_7 (not_7_out, D7);
  not not_8 (not_8_out, D8);
  not not_9 (not_9_out, D9);
  not not_10 (not_10_out, not_2_out);
  not not_11 (not_11_out, not_4_out);
  not not_12 (not_12_out, not_5_out);
  not not_13 (not_13_out, not_6_out);
  nor nor_1 (nor_1_out, not_8_out, not_9_out);
  and and_1 (and_1_out, not_1_out, not_10_out, not_11_out, not_13_out, nor_1_out);
  and and_2 (and_2_out, not_3_out, not_11_out, not_13_out, nor_1_out);
  and and_3 (and_3_out, not_5_out, not_13_out, nor_1_out);
  and and_4 (and_4_out, not_7_out, nor_1_out);
  buf buffer_1 (buffer_1_out, not_9_out);
  and and_5 (and_5_out, not_2_out, not_11_out, not_12_out, nor_1_out);
  and and_6 (and_6_out, not_3_out, not_11_out, not_12_out, nor_1_out);
  and and_7 (and_7_out, not_6_out, nor_1_out);
  and and_8 (and_8_out, not_7_out, nor_1_out);
  and and_9 (and_9_out, not_4_out, nor_1_out);
  and and_10 (and_10_out, not_5_out, nor_1_out);
  and and_11 (and_11_out, not_6_out, nor_1_out);
  and and_12 (and_12_out, not_7_out, nor_1_out);
  nor nor_2 (Q1, and_1_out, and_2_out, and_3_out, and_4_out, buffer_1_out);
  nor nor_3 (Q2, and_5_out, and_6_out, and_7_out, and_8_out);
  nor nor_4 (Q3, and_9_out, and_10_out, and_11_out, and_12_out);
  nor nor_5 (Q4, not_8_out, not_9_out);
endmodule

// 74157
module DIP_74157 (
  input  A1,
  input  B1,
  input  A2,
  input  B2,
  input  A3,
  input  B3,
  input  A4,
  input  B4,
  input  SA,
  input  G,
  output Q1,
  output Q2,
  output Q3,
  output Q4
);

  wire and_1_out, and_2_out, and_3_out, and_4_out, and_5_out, and_6_out, and_7_out, and_8_out, not_1_out,
       not_2_out;

  not not_1 (not_1_out, SA);
  not not_2 (not_2_out, G);
  and and_1 (and_1_out, A1, not_1_out, not_2_out);
  and and_2 (and_2_out, B1, SA, not_2_out);
  and and_3 (and_3_out, A2, not_1_out, not_2_out);
  and and_4 (and_4_out, B2, SA, not_2_out);
  and and_5 (and_5_out, A3, not_1_out, not_2_out);
  and and_6 (and_6_out, B3, SA, not_2_out);
  and and_7 (and_7_out, A4, not_1_out, not_2_out);
  and and_8 (and_8_out, B4, SA, not_2_out);
  or or_1 (Q1, and_1_out, and_2_out);
  or or_2 (Q2, and_3_out, and_4_out);
  or or_3 (Q3, and_5_out, and_6_out);
  or or_4 (Q4, and_7_out, and_8_out);
endmodule

// 74161
module DIP_74161 (
  input  CLK,
  input  CLR_,
  input  LE_,
  input  CEP,
  input  CET,
  input  D1,
  input  D2,
  input  D3,
  input  D4,
  output Q1,
  output Q2,
  output Q3,
  output Q4,
  output TC
);

  wire and_1_out, and_2_out, and_3_out, and_4_out, and_5_out, and_6_out, and_7_out, and_8_out, and_9_out,
       and_10_out, and_11_out, and_12_out, nand_1_out, nand_2_out, nand_3_out, nand_4_out, nand_5_out,
       nand_6_out, nand_7_out, nand_8_out, nand_9_out, nand_10_out, nand_11_out, nand_12_out, nand_13_out,
       nand_14_out, nand_15_out, nand_16_out, nand_17_out, nand_18_out, nand_19_out, nand_20_out,
       nand_21_out, nand_22_out, nand_23_out, nand_24_out, nand_26_out, nand_28_out, nand_30_out,
       nand_32_out, not_1_out, not_2_out, not_3_out, not_4_out, not_5_out, not_6_out, not_7_out, not_8_out,
       not_9_out, not_10_out, not_11_out, or_1_out, or_2_out, or_3_out, or_4_out, xor_1_out, xor_2_out,
       xor_3_out, xor_4_out;

  not not_1 (not_1_out, CLK);
  not not_2 (not_2_out, CLR_);
  and and_1 (and_1_out, LE_, CEP, CET);
  not not_3 (not_3_out, LE_);
  and and_2 (and_2_out, D1, not_3_out);
  and and_3 (and_3_out, Q1, LE_);
  and and_4 (and_4_out, D2, not_3_out);
  and and_5 (and_5_out, Q2, LE_);
  and and_6 (and_6_out, Q1, and_1_out);
  and and_7 (and_7_out, D3, not_3_out);
  and and_8 (and_8_out, Q3, LE_);
  and and_9 (and_9_out, Q2, Q1, and_1_out);
  and and_10 (and_10_out, D4, not_3_out);
  and and_11 (and_11_out, Q4, LE_);
  and and_12 (and_12_out, Q3, Q2, Q1, and_1_out);
  xor xor_1 (xor_1_out, and_3_out, and_1_out);
  xor xor_2 (xor_2_out, and_5_out, and_6_out);
  xor xor_3 (xor_3_out, and_8_out, and_9_out);
  xor xor_4 (xor_4_out, and_11_out, and_12_out);
  or or_1 (or_1_out, and_2_out, xor_1_out);
  or or_2 (or_2_out, and_4_out, xor_2_out);
  or or_3 (or_3_out, and_7_out, xor_3_out);
  or or_4 (or_4_out, and_10_out, xor_4_out);
  nand nand_1 (nand_1_out, or_1_out, not_1_out);
  not not_4 (not_4_out, or_1_out);
  nand nand_2 (nand_2_out, not_1_out, not_4_out);
  nand nand_3 (nand_3_out, or_2_out, not_1_out);
  not not_5 (not_5_out, or_2_out);
  nand nand_4 (nand_4_out, not_1_out, not_5_out);
  nand nand_5 (nand_5_out, or_3_out, not_1_out);
  nand nand_6 (nand_6_out, not_1_out, not_6_out);
  not not_6 (not_6_out, or_3_out);
  nand nand_7 (nand_7_out, or_4_out, not_1_out);
  not not_7 (not_7_out, or_4_out);
  nand nand_8 (nand_8_out, not_1_out, not_7_out);
  nand nand_9 (nand_9_out, nand_1_out, nand_10_out);
  nand nand_10 (nand_10_out, nand_9_out, nand_2_out, not_2_out);
  not not_8 (not_8_out, not_1_out);
  nand nand_11 (nand_11_out, nand_3_out, nand_12_out);
  nand nand_12 (nand_12_out, nand_11_out, nand_4_out, not_2_out);
  not not_9 (not_9_out, not_1_out);
  nand nand_13 (nand_13_out, nand_5_out, nand_14_out);
  nand nand_14 (nand_14_out, nand_13_out, nand_6_out, not_2_out);
  not not_10 (not_10_out, not_1_out);
  nand nand_15 (nand_15_out, nand_7_out, nand_16_out);
  nand nand_16 (nand_16_out, nand_15_out, nand_8_out, not_2_out);
  not not_11 (not_11_out, not_1_out);
  nand nand_17 (nand_17_out, nand_9_out, not_8_out);
  nand nand_18 (nand_18_out, not_8_out, nand_10_out);
  nand nand_19 (nand_19_out, nand_11_out, not_9_out);
  nand nand_20 (nand_20_out, not_9_out, nand_12_out);
  nand nand_21 (nand_21_out, nand_13_out, not_10_out);
  nand nand_22 (nand_22_out, not_10_out, nand_14_out);
  nand nand_23 (nand_23_out, nand_15_out, not_11_out);
  nand nand_24 (nand_24_out, not_11_out, nand_16_out);
  nand nand_25 (Q1, nand_17_out, nand_26_out);
  nand nand_26 (nand_26_out, Q1, nand_18_out, not_2_out);
  nand nand_27 (Q2, nand_19_out, nand_28_out);
  nand nand_28 (nand_28_out, Q2, nand_20_out, not_2_out);
  nand nand_29 (Q3, nand_21_out, nand_30_out);
  nand nand_30 (nand_30_out, Q3, nand_22_out, not_2_out);
  nand nand_31 (Q4, nand_23_out, nand_32_out);
  nand nand_32 (nand_32_out, Q4, nand_24_out, not_2_out);
  and and_13 (TC, Q4, Q3, Q2, Q1, CET);
endmodule

// 74163
module DIP_74163 (
  input  CLK,
  input  CE_,
  input  LE_,
  input  CEP,
  input  CET,
  input  D1,
  input  D2,
  input  D3,
  input  D4,
  output Q1,
  output Q2,
  output Q3,
  output Q4,
  output TC
);

  wire and_1_out, and_2_out, and_3_out, and_4_out, and_5_out, and_6_out, and_7_out, and_8_out, and_9_out,
       and_10_out, and_11_out, and_12_out, and_13_out, nand_1_out, nand_2_out, nand_3_out, nand_4_out,
       nand_5_out, nand_6_out, nand_7_out, nand_8_out, nand_9_out, nand_10_out, nand_11_out, nand_12_out,
       nand_13_out, nand_14_out, nand_15_out, nand_16_out, nand_17_out, nand_18_out, nand_19_out,
       nand_20_out, nand_21_out, nand_22_out, nand_23_out, nand_24_out, nand_26_out, nand_28_out,
       nand_30_out, nand_32_out, not_1_out, not_2_out, not_3_out, not_4_out, not_5_out, not_6_out, not_7_out,
       not_8_out, not_9_out, not_10_out, not_11_out, or_1_out, or_2_out, or_3_out, or_4_out, xor_1_out,
       xor_2_out, xor_3_out, xor_4_out;

  not not_1 (not_1_out, CLK);
  not not_2 (not_2_out, CE_);
  and and_1 (and_1_out, LE_, CEP, CET);
  not not_3 (not_3_out, LE_);
  and and_2 (and_2_out, D1, not_2_out, not_3_out);
  and and_3 (and_3_out, Q1, not_2_out, LE_);
  and and_4 (and_4_out, not_2_out, and_1_out);
  and and_5 (and_5_out, D2, not_2_out, not_3_out);
  and and_6 (and_6_out, Q2, not_2_out, LE_);
  and and_7 (and_7_out, Q1, not_2_out, and_1_out);
  and and_8 (and_8_out, D3, not_2_out, not_3_out);
  and and_9 (and_9_out, Q3, not_2_out, LE_);
  and and_10 (and_10_out, Q2, Q1, and_1_out, not_2_out);
  and and_11 (and_11_out, D4, not_2_out, not_3_out);
  and and_12 (and_12_out, Q4, not_2_out, LE_);
  and and_13 (and_13_out, Q3, Q2, not_2_out, Q1, and_1_out);
  xor xor_1 (xor_1_out, and_3_out, and_4_out);
  xor xor_2 (xor_2_out, and_6_out, and_7_out);
  xor xor_3 (xor_3_out, and_9_out, and_10_out);
  xor xor_4 (xor_4_out, and_12_out, and_13_out);
  or or_1 (or_1_out, and_2_out, xor_1_out);
  or or_2 (or_2_out, and_5_out, xor_2_out);
  or or_3 (or_3_out, and_8_out, xor_3_out);
  or or_4 (or_4_out, and_11_out, xor_4_out);
  nand nand_1 (nand_1_out, or_1_out, not_1_out);
  not not_4 (not_4_out, or_1_out);
  nand nand_2 (nand_2_out, not_1_out, not_4_out);
  nand nand_3 (nand_3_out, or_2_out, not_1_out);
  not not_5 (not_5_out, or_2_out);
  nand nand_4 (nand_4_out, not_1_out, not_5_out);
  nand nand_5 (nand_5_out, or_3_out, not_1_out);
  nand nand_6 (nand_6_out, not_1_out, not_6_out);
  not not_6 (not_6_out, or_3_out);
  nand nand_7 (nand_7_out, or_4_out, not_1_out);
  nand nand_8 (nand_8_out, not_1_out, not_7_out);
  not not_7 (not_7_out, or_4_out);
  nand nand_9 (nand_9_out, nand_1_out, nand_10_out);
  nand nand_10 (nand_10_out, nand_9_out, nand_2_out);
  not not_8 (not_8_out, not_1_out);
  nand nand_11 (nand_11_out, nand_3_out, nand_12_out);
  nand nand_12 (nand_12_out, nand_11_out, nand_4_out);
  not not_9 (not_9_out, not_1_out);
  nand nand_13 (nand_13_out, nand_5_out, nand_14_out);
  nand nand_14 (nand_14_out, nand_13_out, nand_6_out);
  not not_10 (not_10_out, not_1_out);
  nand nand_15 (nand_15_out, nand_7_out, nand_16_out);
  nand nand_16 (nand_16_out, nand_15_out, nand_8_out);
  not not_11 (not_11_out, not_1_out);
  nand nand_17 (nand_17_out, nand_9_out, not_8_out);
  nand nand_18 (nand_18_out, not_8_out, nand_10_out);
  nand nand_19 (nand_19_out, nand_11_out, not_9_out);
  nand nand_20 (nand_20_out, not_9_out, nand_12_out);
  nand nand_21 (nand_21_out, nand_13_out, not_10_out);
  nand nand_22 (nand_22_out, not_10_out, nand_14_out);
  nand nand_23 (nand_23_out, nand_15_out, not_11_out);
  nand nand_24 (nand_24_out, not_11_out, nand_16_out);
  nand nand_25 (Q1, nand_17_out, nand_26_out);
  nand nand_26 (nand_26_out, Q1, nand_18_out);
  nand nand_27 (Q2, nand_19_out, nand_28_out);
  nand nand_28 (nand_28_out, Q2, nand_20_out);
  nand nand_29 (Q3, nand_21_out, nand_30_out);
  nand nand_30 (nand_30_out, Q3, nand_22_out);
  nand nand_31 (Q4, nand_23_out, nand_32_out);
  nand nand_32 (nand_32_out, Q4, nand_24_out);
  and and_14 (TC, Q4, Q3, Q2, Q1, CET);
endmodule

// 74181
module DIP_74181 (
  input  S1,
  input  S2,
  input  S3,
  input  S4,
  input  B4,
  input  A4,
  input  B3,
  input  A3,
  input  B2,
  input  A2,
  input  B1,
  input  A1,
  input  M,
  input  Cn,
  output G,
  output Cn_4,
  output P,
  output Q4,
  output Q3,
  output A_B,
  output Q2,
  output Q1
);

  wire and_1_out, and_2_out, and_3_out, and_4_out, and_5_out, and_6_out, and_7_out, and_8_out, and_9_out,
       and_10_out, and_11_out, and_12_out, and_13_out, and_14_out, and_15_out, and_16_out, and_17_out,
       and_18_out, and_19_out, and_20_out, and_21_out, and_22_out, and_23_out, and_24_out, and_25_out,
       and_26_out, and_27_out, and_28_out, buffer_1_out, buffer_2_out, buffer_3_out, buffer_4_out,
       buffer_5_out, nand_1_out, nand_3_out, nor_1_out, nor_2_out, nor_3_out, nor_4_out, nor_5_out,
       nor_6_out, nor_7_out, nor_8_out, nor_10_out, nor_11_out, nor_12_out, not_1_out, not_2_out, not_3_out,
       not_4_out, not_5_out, xor_1_out, xor_2_out, xor_3_out, xor_4_out;

  not not_1 (not_1_out, B4);
  not not_2 (not_2_out, B3);
  not not_3 (not_3_out, B2);
  not not_4 (not_4_out, B1);
  not not_5 (not_5_out, M);
  and and_1 (and_1_out, B4, S1, A4);
  and and_2 (and_2_out, A4, S2, not_1_out);
  and and_3 (and_3_out, not_1_out, S3);
  and and_4 (and_4_out, S4, B4);
  buf buffer_1 (buffer_1_out, A4);
  and and_5 (and_5_out, B3, S1, A3);
  and and_6 (and_6_out, A3, S2, not_2_out);
  and and_7 (and_7_out, not_2_out, S3);
  and and_8 (and_8_out, S4, B3);
  buf buffer_2 (buffer_2_out, A3);
  and and_9 (and_9_out, B2, S1, A2);
  and and_10 (and_10_out, A2, S2, not_3_out);
  and and_11 (and_11_out, not_3_out, S3);
  and and_12 (and_12_out, S4, B2);
  buf buffer_3 (buffer_3_out, A2);
  and and_13 (and_13_out, B1, S1, A1);
  and and_14 (and_14_out, A1, S2, not_4_out);
  and and_15 (and_15_out, not_4_out, S3);
  and and_16 (and_16_out, S4, B1);
  buf buffer_4 (buffer_4_out, A1);
  nor nor_1 (nor_1_out, and_1_out, and_2_out);
  nor nor_2 (nor_2_out, and_3_out, and_4_out, buffer_1_out);
  nor nor_3 (nor_3_out, and_5_out, and_6_out);
  nor nor_4 (nor_4_out, and_7_out, and_8_out, buffer_2_out);
  nor nor_5 (nor_5_out, and_9_out, and_10_out);
  nor nor_6 (nor_6_out, and_11_out, and_12_out, buffer_3_out);
  nor nor_7 (nor_7_out, and_13_out, and_14_out);
  nor nor_8 (nor_8_out, and_15_out, and_16_out, buffer_4_out);
  xor xor_1 (xor_1_out, nor_1_out, nor_2_out);
  xor xor_2 (xor_2_out, nor_3_out, nor_4_out);
  xor xor_3 (xor_3_out, nor_5_out, nor_6_out);
  xor xor_4 (xor_4_out, nor_7_out, nor_8_out);
  buf buffer_5 (buffer_5_out, nor_2_out);
  and and_17 (and_17_out, nor_1_out, nor_4_out);
  and and_18 (and_18_out, nor_1_out, nor_3_out, nor_6_out);
  and and_19 (and_19_out, nor_1_out, nor_3_out, nor_5_out, nor_8_out);
  nand nand_1 (nand_1_out, nor_1_out, nor_3_out, nor_5_out, nor_7_out, Cn);
  nand nand_2 (P, nor_1_out, nor_3_out, nor_5_out, nor_7_out);
  and and_20 (and_20_out, Cn, nor_7_out, nor_5_out, nor_3_out, not_5_out);
  and and_21 (and_21_out, nor_5_out, nor_3_out, nor_8_out, not_5_out);
  and and_22 (and_22_out, nor_3_out, nor_6_out, not_5_out);
  and and_23 (and_23_out, nor_4_out, not_5_out);
  and and_24 (and_24_out, Cn, nor_7_out, nor_5_out, not_5_out);
  and and_25 (and_25_out, nor_5_out, nor_8_out, not_5_out);
  and and_26 (and_26_out, nor_6_out, not_5_out);
  and and_27 (and_27_out, Cn, nor_7_out, not_5_out);
  and and_28 (and_28_out, nor_8_out, not_5_out);
  nand nand_3 (nand_3_out, Cn, not_5_out);
  nor nor_9 (G, buffer_5_out, and_17_out, and_18_out, and_19_out);
  nor nor_10 (nor_10_out, and_20_out, and_21_out, and_22_out, and_23_out);
  nor nor_11 (nor_11_out, and_24_out, and_25_out, and_26_out);
  nor nor_12 (nor_12_out, and_27_out, and_28_out);
  nor nor_13 (Cn_4, G, nand_1_out);
  xor xor_5 (Q4, xor_1_out, nor_10_out);
  xor xor_6 (Q3, xor_2_out, nor_11_out);
  xor xor_7 (Q2, xor_3_out, nor_12_out);
  xor xor_8 (Q1, xor_4_out, nand_3_out);
  and and_29 (A_B, Q3, Q4, Q1, Q2);
endmodule

// 74244
module DIP_74244 (
  input  A1,
  input  A2,
  input  A3,
  input  A4,
  input  OEA,
  input  B1,
  input  B2,
  input  B3,
  input  B4,
  input  OEB,
  output Q1,
  output Q2,
  output Q3,
  output Q4,
  output R1,
  output R2,
  output R3,
  output R4
);

  wire not_1_out, not_2_out;

  not not_1 (not_1_out, OEA);
  not not_2 (not_2_out, OEB);
  assign Q1 = not_1_out ? A1 : 1'bz;  // Controlled_Buffer controlled_buffer_1
  assign Q2 = not_1_out ? A2 : 1'bz;  // Controlled_Buffer controlled_buffer_2
  assign Q3 = not_1_out ? A3 : 1'bz;  // Controlled_Buffer controlled_buffer_3
  assign Q4 = not_1_out ? A4 : 1'bz;  // Controlled_Buffer controlled_buffer_4
  assign R1 = not_2_out ? B1 : 1'bz;  // Controlled_Buffer controlled_buffer_5
  assign R2 = not_2_out ? B2 : 1'bz;  // Controlled_Buffer controlled_buffer_6
  assign R3 = not_2_out ? B3 : 1'bz;  // Controlled_Buffer controlled_buffer_7
  assign R4 = not_2_out ? B4 : 1'bz;  // Controlled_Buffer controlled_buffer_8
endmodule

// 74247
module DIP_74247 (
  input  LT_,
  input  D1,
  input  D2,
  input  D3,
  input  D4,
  input  RBI_,
  input  BI,
  output Qa,
  output Qb,
  output Qc,
  output Qd,
  output Qe,
  output Qf,
  output Qg
);

  wire and_1_out, and_2_out, and_3_out, and_4_out, and_5_out, and_6_out, and_7_out, and_8_out, and_9_out,
       and_10_out, and_11_out, and_12_out, and_13_out, and_14_out, and_15_out, and_16_out, and_17_out,
       buffer_1_out, buffer_2_out, nand_1_out, nand_2_out, nand_3_out, nand_4_out, nand_5_out, nand_6_out,
       nand_7_out, nand_8_out, nor_1_out, nor_2_out, nor_3_out, nor_4_out, nor_5_out, nor_6_out, nor_7_out,
       not_1_out, not_2_out;

  buf buffer_1 (buffer_1_out, LT_);
  not not_1 (not_1_out, RBI_);
  nand nand_1 (nand_1_out, not_1_out, buffer_1_out, not_2_out, nand_5_out, nand_4_out, nand_3_out);
  nand nand_2 (nand_2_out, nand_1_out, not_2_out);
  nand nand_3 (nand_3_out, D1, buffer_1_out);
  nand nand_4 (nand_4_out, D2, buffer_1_out);
  nand nand_5 (nand_5_out, D3, buffer_1_out);
  not not_2 (not_2_out, D4);
  nand nand_6 (nand_6_out, nand_1_out, nand_4_out);
  nand nand_7 (nand_7_out, nand_1_out, nand_5_out);
  nand nand_8 (nand_8_out, nand_1_out, nand_3_out);
  and and_1 (and_1_out, nand_6_out, nand_2_out);
  and and_2 (and_2_out, nand_3_out, nand_4_out, nand_7_out);
  and and_3 (and_3_out, nand_8_out, nand_4_out, nand_5_out, not_2_out);
  and and_4 (and_4_out, nand_6_out, nand_2_out);
  and and_5 (and_5_out, nand_8_out, nand_4_out, nand_7_out);
  and and_6 (and_6_out, nand_3_out, nand_6_out, nand_7_out);
  and and_7 (and_7_out, nand_7_out, nand_2_out);
  and and_8 (and_8_out, nand_3_out, nand_6_out, nand_5_out);
  and and_9 (and_9_out, nand_8_out, nand_4_out, nand_5_out, not_2_out);
  and and_10 (and_10_out, nand_3_out, nand_4_out, nand_7_out);
  and and_11 (and_11_out, nand_8_out, nand_6_out, nand_7_out);
  buf buffer_2 (buffer_2_out, nand_8_out);
  and and_12 (and_12_out, nand_4_out, nand_7_out);
  and and_13 (and_13_out, nand_8_out, nand_6_out);
  and and_14 (and_14_out, nand_6_out, nand_5_out);
  and and_15 (and_15_out, nand_8_out, nand_5_out, not_2_out);
  and and_16 (and_16_out, nand_8_out, nand_6_out, nand_7_out);
  and and_17 (and_17_out, nand_4_out, nand_5_out, not_2_out, buffer_1_out);
  nor nor_1 (nor_1_out, and_1_out, and_2_out, and_3_out);
  nor nor_2 (nor_2_out, and_4_out, and_5_out, and_6_out);
  nor nor_3 (nor_3_out, and_7_out, and_8_out);
  nor nor_4 (nor_4_out, and_9_out, and_10_out, and_11_out);
  nor nor_5 (nor_5_out, buffer_2_out, and_12_out);
  nor nor_6 (nor_6_out, and_13_out, and_14_out, and_15_out);
  nor nor_7 (nor_7_out, and_16_out, and_17_out);
  not not_3 (Qa, nor_1_out);
  not not_4 (Qb, nor_2_out);
  not not_5 (Qc, nor_3_out);
  not not_6 (Qd, nor_4_out);
  not not_7 (Qe, nor_5_out);
  not not_8 (Qf, nor_6_out);
  not not_9 (Qg, nor_7_out);
endmodule

// 74283
module DIP_74283 (
  input  CIN,
  input  A1,
  input  B1,
  input  A2,
  input  B2,
  input  A3,
  input  B3,
  input  A4,
  input  B4,
  output Q1,
  output Q2,
  output Q3,
  output Q4,
  output COUT
);

  wire and_1_out, and_2_out, and_3_out, and_4_out, and_5_out, and_6_out, and_7_out, and_8_out, and_9_out,
       and_10_out, and_11_out, and_12_out, and_13_out, and_14_out, nand_1_out, nand_2_out, nand_3_out,
       nand_4_out, nor_1_out, nor_2_out, nor_3_out, nor_4_out, nor_5_out, nor_6_out, nor_7_out, not_1_out,
       not_2_out, not_3_out, not_4_out, not_5_out, not_6_out;

  not not_1 (not_1_out, CIN);
  nor nor_1 (nor_1_out, A1, B1);
  nand nand_1 (nand_1_out, A1, B1);
  nor nor_2 (nor_2_out, A2, B2);
  nand nand_2 (nand_2_out, A2, B2);
  nor nor_3 (nor_3_out, A3, B3);
  nand nand_3 (nand_3_out, A3, B3);
  nor nor_4 (nor_4_out, A4, B4);
  nand nand_4 (nand_4_out, A4, B4);
  not not_2 (not_2_out, not_1_out);
  not not_3 (not_3_out, nor_1_out);
  and and_1 (and_1_out, not_1_out, nand_1_out);
  not not_4 (not_4_out, nor_2_out);
  and and_2 (and_2_out, not_1_out, nand_1_out, nand_2_out);
  and and_3 (and_3_out, nand_2_out, nor_1_out);
  not not_5 (not_5_out, nor_3_out);
  and and_4 (and_4_out, not_1_out, nand_1_out, nand_2_out, nand_3_out);
  and and_5 (and_5_out, nand_2_out, nand_3_out, nor_1_out);
  and and_6 (and_6_out, nand_3_out, nor_2_out);
  not not_6 (not_6_out, nor_4_out);
  and and_7 (and_7_out, not_1_out, nand_1_out, nand_2_out, nand_3_out, nand_4_out);
  and and_8 (and_8_out, nand_2_out, nand_3_out, nand_4_out, nor_1_out);
  and and_9 (and_9_out, nand_3_out, nand_4_out, nor_2_out);
  and and_10 (and_10_out, nand_4_out, nor_3_out);
  and and_11 (and_11_out, not_3_out, nand_1_out);
  nor nor_5 (nor_5_out, and_1_out, nor_1_out);
  and and_12 (and_12_out, not_4_out, nand_2_out);
  nor nor_6 (nor_6_out, and_2_out, and_3_out, nor_2_out);
  and and_13 (and_13_out, not_5_out, nand_3_out);
  nor nor_7 (nor_7_out, and_4_out, and_5_out, and_6_out, nor_3_out);
  and and_14 (and_14_out, not_6_out, nand_4_out);
  nor nor_8 (COUT, and_7_out, and_8_out, and_9_out, and_10_out, nor_4_out);
  xor xor_1 (Q1, not_2_out, and_11_out);
  xor xor_2 (Q2, nor_5_out, and_12_out);
  xor xor_3 (Q3, nor_6_out, and_13_out);
  xor xor_4 (Q4, nor_7_out, and_14_out);
endmodule

// 74373
module DIP_74373 (
  input  OE,
  input  LE,
  input  D1,
  input  D2,
  input  D3,
  input  D4,
  input  D5,
  input  D6,
  input  D7,
  input  D8,
  output Q1,
  output Q2,
  output Q3,
  output Q4,
  output Q5,
  output Q6,
  output Q7,
  output Q8
);

  wire buffer_1_out, nand_1_out, nand_2_out, nand_3_out, nand_4_out, nand_5_out, nand_6_out, nand_7_out,
       nand_8_out, nand_9_out, nand_10_out, nand_11_out, nand_12_out, nand_13_out, nand_14_out, nand_15_out,
       nand_16_out, nand_17_out, nand_18_out, nand_19_out, nand_20_out, nand_21_out, nand_22_out,
       nand_23_out, nand_24_out, nand_25_out, nand_26_out, nand_27_out, nand_28_out, nand_29_out,
       nand_30_out, nand_31_out, nand_32_out, not_1_out;

  not not_1 (not_1_out, OE);
  buf buffer_1 (buffer_1_out, LE);
  nand nand_1 (nand_1_out, D1, buffer_1_out);
  nand nand_2 (nand_2_out, nand_1_out, buffer_1_out);
  nand nand_3 (nand_3_out, D2, buffer_1_out);
  nand nand_4 (nand_4_out, nand_3_out, buffer_1_out);
  nand nand_5 (nand_5_out, D3, buffer_1_out);
  nand nand_6 (nand_6_out, nand_5_out, buffer_1_out);
  nand nand_7 (nand_7_out, D4, buffer_1_out);
  nand nand_8 (nand_8_out, nand_7_out, buffer_1_out);
  nand nand_9 (nand_9_out, D5, buffer_1_out);
  nand nand_10 (nand_10_out, nand_9_out, buffer_1_out);
  nand nand_11 (nand_11_out, D6, buffer_1_out);
  nand nand_12 (nand_12_out, nand_11_out, buffer_1_out);
  nand nand_13 (nand_13_out, D7, buffer_1_out);
  nand nand_14 (nand_14_out, nand_13_out, buffer_1_out);
  nand nand_15 (nand_15_out, D8, buffer_1_out);
  nand nand_16 (nand_16_out, nand_15_out, buffer_1_out);
  nand nand_17 (nand_17_out, nand_1_out, nand_18_out);
  nand nand_18 (nand_18_out, nand_17_out, nand_2_out);
  nand nand_19 (nand_19_out, nand_3_out, nand_20_out);
  nand nand_20 (nand_20_out, nand_19_out, nand_4_out);
  nand nand_21 (nand_21_out, nand_5_out, nand_22_out);
  nand nand_22 (nand_22_out, nand_21_out, nand_6_out);
  nand nand_23 (nand_23_out, nand_7_out, nand_24_out);
  nand nand_24 (nand_24_out, nand_23_out, nand_8_out);
  nand nand_25 (nand_25_out, nand_9_out, nand_26_out);
  nand nand_26 (nand_26_out, nand_25_out, nand_10_out);
  nand nand_27 (nand_27_out, nand_11_out, nand_28_out);
  nand nand_28 (nand_28_out, nand_27_out, nand_12_out);
  nand nand_29 (nand_29_out, nand_13_out, nand_30_out);
  nand nand_30 (nand_30_out, nand_29_out, nand_14_out);
  nand nand_31 (nand_31_out, nand_15_out, nand_32_out);
  nand nand_32 (nand_32_out, nand_31_out, nand_16_out);
  assign Q1 = not_1_out ? nand_17_out : 1'bz;  // Controlled_Buffer controlled_buffer_1
  assign Q2 = not_1_out ? nand_19_out : 1'bz;  // Controlled_Buffer controlled_buffer_2
  assign Q3 = not_1_out ? nand_21_out : 1'bz;  // Controlled_Buffer controlled_buffer_3
  assign Q4 = not_1_out ? nand_23_out : 1'bz;  // Controlled_Buffer controlled_buffer_4
  assign Q5 = not_1_out ? nand_25_out : 1'bz;  // Controlled_Buffer controlled_buffer_5
  assign Q6 = not_1_out ? nand_27_out : 1'bz;  // Controlled_Buffer controlled_buffer_6
  assign Q7 = not_1_out ? nand_29_out : 1'bz;  // Controlled_Buffer controlled_buffer_7
  assign Q8 = not_1_out ? nand_31_out : 1'bz;  // Controlled_Buffer controlled_buffer_8
endmodule

// 74377
module DIP_74377 (
  input  CLKEN,
  input  CLK,
  input  _1D,
  input  _2D,
  input  _3D,
  input  _4D,
  input  _5D,
  input  _6D,
  input  _7D,
  input  _8D,
  output _1Q,
  output _2Q,
  output _3Q,
  output _4Q,
  output _5Q,
  output _6Q,
  output _7Q,
  output _8Q
);

  wire and_1_out, not_1_out, not_2_out, or_1_out, or_2_out;

  not not_1 (not_1_out, CLKEN);
  not not_2 (not_2_out, CLK);
  or or_1 (or_1_out, not_1_out, or_2_out);
  or or_2 (or_2_out, or_1_out, not_2_out);
  D_Flip_Flop d_ff_1 (.clk(and_1_out), .D(_1D), .Q(_1Q));  // open: Qn, preset, en, reset
  D_Flip_Flop d_ff_2 (.clk(and_1_out), .D(_2D), .Q(_2Q));  // open: Qn, preset, en, reset
  D_Flip_Flop d_ff_3 (.clk(and_1_out), .D(_3D), .Q(_3Q));  // open: Qn, preset, en, reset
  D_Flip_Flop d_ff_4 (.clk(and_1_out), .D(_4D), .Q(_4Q));  // open: Qn, preset, en, reset
  D_Flip_Flop d_ff_5 (.clk(and_1_out), .D(_5D), .Q(_5Q));  // open: Qn, preset, en, reset
  D_Flip_Flop d_ff_6 (.clk(and_1_out), .D(_6D), .Q(_6Q));  // open: Qn, preset, en, reset
  D_Flip_Flop d_ff_7 (.clk(and_1_out), .D(_7D), .Q(_7Q));  // open: Qn, preset, en, reset
  D_Flip_Flop d_ff_8 (.clk(and_1_out), .D(_8D), .Q(_8Q));  // open: Qn, preset, en, reset
  and and_1 (and_1_out, or_1_out, not_2_out);
endmodule

// 74595
module DIP_74595 (
  input  D,
  input  OE,
  input  LCLK,
  input  SCLK,
  input  RST,
  output QA,
  output QB,
  output QC,
  output QD,
  output QE,
  output QF,
  output QG,
  output QH,
  output SQH
);

  wire d_ff_1_q, d_ff_2_q, d_ff_3_q, d_ff_4_q, d_ff_5_q, d_ff_6_q, d_ff_7_q, d_ff_9_q, d_ff_10_q, d_ff_11_q,
       d_ff_12_q, d_ff_13_q, d_ff_14_q, d_ff_15_q, d_ff_16_q, not_1_out;

  not not_1 (not_1_out, OE);
  D_Flip_Flop d_ff_1 (.clk(SCLK), .D(D), .Q(d_ff_1_q), .reset(RST));  // open: Qn, preset, en
  D_Flip_Flop d_ff_2 (.clk(SCLK), .D(d_ff_1_q), .Q(d_ff_2_q), .reset(RST));  // open: Qn, preset, en
  D_Flip_Flop d_ff_3 (.clk(SCLK), .D(d_ff_2_q), .Q(d_ff_3_q), .reset(RST));  // open: Qn, preset, en
  D_Flip_Flop d_ff_4 (.clk(SCLK), .D(d_ff_3_q), .Q(d_ff_4_q), .reset(RST));  // open: Qn, preset, en
  D_Flip_Flop d_ff_5 (.clk(SCLK), .D(d_ff_4_q), .Q(d_ff_5_q), .reset(RST));  // open: Qn, preset, en
  D_Flip_Flop d_ff_6 (.clk(SCLK), .D(d_ff_5_q), .Q(d_ff_6_q), .reset(RST));  // open: Qn, preset, en
  D_Flip_Flop d_ff_7 (.clk(SCLK), .D(d_ff_6_q), .Q(d_ff_7_q), .reset(RST));  // open: Qn, preset, en
  D_Flip_Flop d_ff_8 (.clk(SCLK), .D(d_ff_7_q), .Q(SQH), .reset(RST));  // open: Qn, preset, en
  D_Flip_Flop d_ff_9 (.clk(LCLK), .D(d_ff_1_q), .Q(d_ff_9_q));  // open: Qn, preset, en, reset
  D_Flip_Flop d_ff_10 (.clk(LCLK), .D(d_ff_2_q), .Q(d_ff_10_q));  // open: Qn, preset, en, reset
  D_Flip_Flop d_ff_11 (.clk(LCLK), .D(d_ff_3_q), .Q(d_ff_11_q));  // open: Qn, preset, en, reset
  D_Flip_Flop d_ff_12 (.clk(LCLK), .D(d_ff_4_q), .Q(d_ff_12_q));  // open: Qn, preset, en, reset
  D_Flip_Flop d_ff_13 (.clk(LCLK), .D(d_ff_5_q), .Q(d_ff_13_q));  // open: Qn, preset, en, reset
  D_Flip_Flop d_ff_14 (.clk(LCLK), .D(d_ff_6_q), .Q(d_ff_14_q));  // open: Qn, preset, en, reset
  D_Flip_Flop d_ff_15 (.clk(LCLK), .D(d_ff_7_q), .Q(d_ff_15_q));  // open: Qn, preset, en, reset
  D_Flip_Flop d_ff_16 (.clk(LCLK), .D(SQH), .Q(d_ff_16_q));  // open: Qn, preset, en, reset
  assign QA = not_1_out ? d_ff_9_q : 1'bz;  // Controlled_Buffer controlled_buffer_1
  assign QB = not_1_out ? d_ff_10_q : 1'bz;  // Controlled_Buffer controlled_buffer_2
  assign QC = not_1_out ? d_ff_11_q : 1'bz;  // Controlled_Buffer controlled_buffer_3
  assign QD = not_1_out ? d_ff_12_q : 1'bz;  // Controlled_Buffer controlled_buffer_4
  assign QE = not_1_out ? d_ff_13_q : 1'bz;  // Controlled_Buffer controlled_buffer_5
  assign QF = not_1_out ? d_ff_14_q : 1'bz;  // Controlled_Buffer controlled_buffer_6
  assign QG = not_1_out ? d_ff_15_q : 1'bz;  // Controlled_Buffer controlled_buffer_7
  assign QH = not_1_out ? d_ff_16_q : 1'bz;  // Controlled_Buffer controlled_buffer_8
endmodule

// 74670
module DIP_74670 (
  input  RE,
  input  RA,
  input  RB,
  input  WE,
  input  WA,
  input  WB,
  input  D1,
  input  D2,
  input  D3,
  input  D4,
  output Q1,
  output Q2,
  output Q3,
  output Q4
);

  wire and_1_out, and_2_out, and_3_out, and_4_out, and_5_out, and_6_out, and_7_out, and_8_out, and_9_out,
       and_10_out, and_11_out, and_12_out, and_13_out, and_14_out, and_15_out, and_16_out, and_17_out,
       and_18_out, and_19_out, and_20_out, and_21_out, and_22_out, d_ff_1_q, d_ff_2_q, d_ff_3_q, d_ff_4_q,
       d_ff_5_q, d_ff_6_q, d_ff_7_q, d_ff_8_q, d_ff_9_q, d_ff_10_q, d_ff_11_q, d_ff_12_q, d_ff_13_q,
       d_ff_14_q, d_ff_15_q, d_ff_16_q, nor_1_out, nor_2_out, nor_3_out, nor_4_out, not_1_out, not_2_out,
       not_3_out, not_4_out, not_5_out, not_6_out, not_7_out, not_8_out, not_9_out, not_10_out, not_11_out,
       not_12_out, not_13_out, not_14_out;

  not not_1 (not_1_out, RE);
  not not_2 (not_2_out, RA);
  not not_3 (not_3_out, RB);
  not not_4 (not_4_out, WE);
  not not_5 (not_5_out, WA);
  not not_6 (not_6_out, WB);
  and and_1 (and_1_out, not_6_out, and_2_out);
  not not_7 (not_7_out, D1);
  not not_8 (not_8_out, D2);
  not not_9 (not_9_out, D3);
  not not_10 (not_10_out, D4);
  not not_11 (not_11_out, not_6_out);
  and and_2 (and_2_out, not_5_out, not_4_out);
  and and_3 (and_3_out, and_2_out, not_11_out);
  D_Flip_Flop #(.trigger("high")) d_ff_1 (.clk(and_1_out), .D(not_7_out), .Q(d_ff_1_q));  // open: Qn, preset, en, reset
  D_Flip_Flop #(.trigger("high")) d_ff_2 (.clk(and_1_out), .D(not_8_out), .Q(d_ff_2_q));  // open: Qn, preset, en, reset
  D_Flip_Flop #(.trigger("high")) d_ff_3 (.clk(and_1_out), .D(not_9_out), .Q(d_ff_3_q));  // open: Qn, preset, en, reset
  D_Flip_Flop #(.trigger("high")) d_ff_4 (
    .clk(and_1_out), .D(not_10_out), .Q(d_ff_4_q));  // open: Qn, preset, en, reset
  not not_12 (not_12_out, not_5_out);
  and and_4 (and_4_out, not_6_out, and_5_out);
  D_Flip_Flop #(.trigger("high")) d_ff_5 (.clk(and_3_out), .D(not_7_out), .Q(d_ff_5_q));  // open: Qn, preset, en, reset
  D_Flip_Flop #(.trigger("high")) d_ff_6 (.clk(and_3_out), .D(not_8_out), .Q(d_ff_6_q));  // open: Qn, preset, en, reset
  D_Flip_Flop #(.trigger("high")) d_ff_7 (.clk(and_3_out), .D(not_9_out), .Q(d_ff_7_q));  // open: Qn, preset, en, reset
  D_Flip_Flop #(.trigger("high")) d_ff_8 (
    .clk(and_3_out), .D(not_10_out), .Q(d_ff_8_q));  // open: Qn, preset, en, reset
  and and_5 (and_5_out, not_12_out, not_4_out);
  and and_6 (and_6_out, and_5_out, not_11_out);
  D_Flip_Flop #(.trigger("high")) d_ff_9 (.clk(and_4_out), .D(not_7_out), .Q(d_ff_9_q));  // open: Qn, preset, en, reset
  D_Flip_Flop #(.trigger("high")) d_ff_10 (
    .clk(and_4_out), .D(not_8_out), .Q(d_ff_10_q));  // open: Qn, preset, en, reset
  D_Flip_Flop #(.trigger("high")) d_ff_11 (
    .clk(and_4_out), .D(not_9_out), .Q(d_ff_11_q));  // open: Qn, preset, en, reset
  D_Flip_Flop #(.trigger("high")) d_ff_12 (
    .clk(and_4_out), .D(not_10_out), .Q(d_ff_12_q));  // open: Qn, preset, en, reset
  not not_13 (not_13_out, not_3_out);
  D_Flip_Flop #(.trigger("high")) d_ff_13 (
    .clk(and_6_out), .D(not_7_out), .Q(d_ff_13_q));  // open: Qn, preset, en, reset
  D_Flip_Flop #(.trigger("high")) d_ff_14 (
    .clk(and_6_out), .D(not_8_out), .Q(d_ff_14_q));  // open: Qn, preset, en, reset
  D_Flip_Flop #(.trigger("high")) d_ff_15 (
    .clk(and_6_out), .D(not_9_out), .Q(d_ff_15_q));  // open: Qn, preset, en, reset
  D_Flip_Flop #(.trigger("high")) d_ff_16 (
    .clk(and_6_out), .D(not_10_out), .Q(d_ff_16_q));  // open: Qn, preset, en, reset
  not not_14 (not_14_out, not_2_out);
  and and_7 (and_7_out, d_ff_1_q, not_3_out, not_2_out);
  and and_8 (and_8_out, d_ff_5_q, not_3_out, not_14_out);
  and and_9 (and_9_out, d_ff_9_q, not_13_out, not_2_out);
  and and_10 (and_10_out, d_ff_13_q, not_13_out, not_14_out);
  and and_11 (and_11_out, d_ff_2_q, not_3_out, not_2_out);
  and and_12 (and_12_out, d_ff_6_q, not_3_out, not_14_out);
  and and_13 (and_13_out, d_ff_10_q, not_13_out, not_2_out);
  and and_14 (and_14_out, d_ff_14_q, not_13_out, not_14_out);
  and and_15 (and_15_out, d_ff_3_q, not_3_out, not_2_out);
  and and_16 (and_16_out, d_ff_7_q, not_3_out, not_14_out);
  and and_17 (and_17_out, d_ff_11_q, not_13_out, not_2_out);
  and and_18 (and_18_out, d_ff_15_q, not_13_out, not_14_out);
  and and_19 (and_19_out, d_ff_4_q, not_3_out, not_2_out);
  and and_20 (and_20_out, d_ff_8_q, not_3_out, not_14_out);
  and and_21 (and_21_out, d_ff_12_q, not_13_out, not_2_out);
  and and_22 (and_22_out, d_ff_16_q, not_13_out, not_14_out);
  nor nor_1 (nor_1_out, and_7_out, and_8_out, and_9_out, and_10_out);
  assign Q1 = not_1_out ? nor_1_out : 1'bz;  // Controlled_Buffer controlled_buffer_1
  assign Q2 = not_1_out ? nor_2_out : 1'bz;  // Controlled_Buffer controlled_buffer_2
  nor nor_2 (nor_2_out, and_11_out, and_12_out, and_13_out, and_14_out);
  nor nor_3 (nor_3_out, and_15_out, and_16_out, and_17_out, and_18_out);
  assign Q3 = not_1_out ? nor_3_out : 1'bz;  // Controlled_Buffer controlled_buffer_3
  assign Q4 = not_1_out ? nor_4_out : 1'bz;  // Controlled_Buffer controlled_buffer_4
  nor nor_4 (nor_4_out, and_19_out, and_20_out, and_21_out, and_22_out);
endmodule

// 744075
module DIP_744075 (
  input  A1,
  input  B1,
  input  C1,
  input  A2,
  input  B2,
  input  C2,
  input  A3,
  input  B3,
  input  C3,
  output Q1,
  output Q2,
  output Q3
);

  or or_1 (Q1, A1, B1, C1);
  or or_2 (Q2, A2, B2, C2);
  or or_3 (Q3, A3, B3, C3);
endmodule

// 744078
module DIP_744078 (
  input  A,
  input  B,
  input  C,
  input  D,
  input  E,
  input  F,
  input  G,
  input  H,
  output Q,
  output R
);

  nor nor_1 (Q, A, B, C, D, E, F, G, H);
  not not_1 (R, Q);
endmodule

// 744511
module DIP_744511 (
  input  LT_,
  input  D1,
  input  D2,
  input  D3,
  input  D4,
  input  LE,
  input  BL_,
  output Qa,
  output Qb,
  output Qc,
  output Qd,
  output Qe,
  output Qf,
  output Qg
);

  wire nand_1_out, nand_2_out, nand_3_out, nand_4_out, nand_5_out, nand_6_out, nand_7_out, nand_8_out,
       nand_9_out, nand_10_out, nand_11_out, nand_12_out, nand_13_out, nand_14_out, nand_15_out, nand_16_out,
       nand_17_out, nand_18_out, nand_19_out, nand_20_out, nand_21_out, nand_22_out, nand_23_out,
       nand_24_out, nand_25_out, nand_26_out, nand_27_out, nand_28_out, nand_29_out, nand_30_out,
       nand_31_out, nand_32_out, nand_33_out, nand_34_out, not_1_out, or_1_out;

  nand nand_1 (nand_1_out, D1, LE);
  nand nand_2 (nand_2_out, nand_1_out, nand_3_out);
  nand nand_3 (nand_3_out, nand_2_out, nand_4_out);
  nand nand_4 (nand_4_out, nand_1_out, LE);
  nand nand_5 (nand_5_out, nand_6_out, nand_7_out);
  nand nand_6 (nand_6_out, D2, LE);
  nand nand_7 (nand_7_out, nand_5_out, nand_8_out);
  nand nand_8 (nand_8_out, nand_6_out, LE);
  nand nand_9 (nand_9_out, D3, LE);
  nand nand_10 (nand_10_out, nand_9_out, nand_12_out);
  nand nand_11 (nand_11_out, nand_9_out, LE);
  nand nand_12 (nand_12_out, nand_10_out, nand_11_out);
  nand nand_13 (nand_13_out, nand_14_out, nand_16_out);
  nand nand_14 (nand_14_out, D4, LE);
  nand nand_15 (nand_15_out, nand_14_out, LE);
  nand nand_16 (nand_16_out, nand_13_out, nand_15_out);
  or or_1 (or_1_out, nand_5_out, nand_10_out);
  nand nand_17 (nand_17_out, nand_10_out, nand_5_out, nand_3_out);
  nand nand_18 (nand_18_out, nand_10_out, nand_2_out, nand_7_out);
  nand nand_19 (nand_19_out, nand_5_out, nand_3_out, nand_12_out);
  nand nand_20 (nand_20_out, nand_2_out, nand_12_out, nand_7_out);
  nand nand_21 (nand_21_out, nand_10_out, nand_7_out, nand_3_out);
  nand nand_22 (nand_22_out, nand_5_out, nand_12_out);
  nand nand_23 (nand_23_out, nand_16_out, nand_12_out, nand_7_out, nand_3_out);
  nand nand_24 (nand_24_out, nand_10_out, nand_5_out, nand_2_out);
  nand nand_25 (nand_25_out, nand_7_out, nand_12_out, nand_16_out, nand_2_out);
  nand nand_26 (nand_26_out, or_1_out, nand_13_out);
  not not_1 (not_1_out, nand_27_out);
  nand nand_27 (nand_27_out, nand_26_out, BL_);
  nand nand_28 (nand_28_out, nand_17_out, not_1_out, nand_21_out, nand_25_out);
  nand nand_29 (nand_29_out, nand_18_out, nand_17_out, not_1_out);
  nand nand_30 (nand_30_out, nand_19_out, not_1_out);
  nand nand_31 (nand_31_out, nand_20_out, nand_21_out, not_1_out, nand_24_out);
  nand nand_32 (nand_32_out, nand_21_out, not_1_out, nand_3_out);
  nand nand_33 (nand_33_out, nand_22_out, not_1_out, nand_24_out, nand_25_out);
  nand nand_34 (nand_34_out, nand_23_out, nand_25_out, not_1_out, nand_24_out);
  nand nand_35 (Qa, nand_28_out, LT_);
  nand nand_36 (Qb, nand_29_out, LT_);
  nand nand_37 (Qc, nand_30_out, LT_);
  nand nand_38 (Qd, nand_31_out, LT_);
  nand nand_39 (Qe, nand_32_out, LT_);
  nand nand_40 (Qf, nand_33_out, LT_);
  nand nand_41 (Qg, nand_34_out, LT_);
endmodule

module D_Latch (
);

  wire nand_1_out, nand_2_out, nand_3_out, nand_4_out, nand_5_out, nand_6_out, nand_7_out, nand_8_out,
       nand_9_out, nand_10_out, nand_11_out, nand_12_out, nand_13_out, nand_14_out, nand_15_out, nand_16_out,
       nand_17_out, nand_18_out, nand_19_out, nand_20_out, nand_21_out, nand_22_out, nand_23_out,
       nand_24_out, not_1_out, not_2_out, not_3_out, not_4_out, not_5_out, not_6_out, undriven, undriven_2,
       undriven_3, undriven_4, undriven_5, undriven_6, undriven_7, undriven_8, undriven_9;

  not not_1 (not_1_out, undriven);
  not not_2 (not_2_out, undriven_2);
  not not_3 (not_3_out, undriven_4);
  nand nand_1 (nand_1_out, undriven, undriven_5);
  nand nand_2 (nand_2_out, undriven_5, not_1_out);
  not not_4 (not_4_out, undriven_5);
  nand nand_3 (nand_3_out, undriven_2, undriven_3);
  nand nand_4 (nand_4_out, undriven_3, not_2_out);
  not not_5 (not_5_out, undriven_3);
  nand nand_5 (nand_5_out, undriven_4, undriven_6);
  nand nand_6 (nand_6_out, undriven_6, not_3_out);
  not not_6 (not_6_out, undriven_6);
  nand nand_7 (nand_7_out, nand_1_out, nand_8_out);
  nand nand_8 (nand_8_out, nand_7_out, nand_2_out);
  nand nand_9 (nand_9_out, nand_3_out, nand_10_out);
  nand nand_10 (nand_10_out, nand_9_out, nand_4_out, undriven_9);
  nand nand_11 (nand_11_out, undriven_7, nand_5_out, nand_12_out);
  nand nand_12 (nand_12_out, nand_11_out, nand_6_out, undriven_8);
  nand nand_13 (nand_13_out, nand_7_out, not_4_out);
  nand nand_14 (nand_14_out, nand_13_out, nand_16_out);
  nand nand_15 (nand_15_out, not_4_out, nand_8_out);
  nand nand_16 (nand_16_out, nand_14_out, nand_15_out);
  nand nand_17 (nand_17_out, nand_9_out, not_5_out);
  nand nand_18 (nand_18_out, nand_17_out, nand_19_out);
  nand nand_19 (nand_19_out, nand_18_out, nand_20_out, undriven_9);
  nand nand_20 (nand_20_out, not_5_out, nand_10_out);
  nand nand_21 (nand_21_out, nand_11_out, not_6_out);
  nand nand_22 (nand_22_out, undriven_7, nand_21_out, nand_24_out);
  nand nand_23 (nand_23_out, not_6_out, nand_12_out);
  nand nand_24 (nand_24_out, nand_22_out, nand_23_out, undriven_8);
endmodule
