// Logisim project 74x299.circ as structural Verilog: 1 circuit, main circuit 74x299
module _74x299 (
  input  G0,
  input  G1,
  input  CLK,
  input  SR,
  input  S0,
  input  S1,
  input  A,
  input  B,
  input  C,
  input  D,
  input  E,
  input  F,
  input  G,
  input  H,
  input  SL,
  output QA_prime,
  output QA,
  output QB,
  output QC,
  output QD,
  output QE,
  output QF,
  output QG,
  output QH,
  output QH_prime
);

  wire and_1_out, and_2_out, and_3_out, and_4_out, and_5_out, and_6_out, and_7_out, and_8_out, and_9_out,
       and_10_out, and_11_out, and_12_out, and_13_out, and_14_out, and_15_out, and_16_out, and_17_out,
       and_18_out, and_19_out, and_20_out, and_21_out, and_22_out, and_23_out, and_24_out, and_25_out,
       and_26_out, and_27_out, and_28_out, and_29_out, and_30_out, and_31_out, and_32_out, and_33_out,
       nand_1_out, nand_2_out, nand_3_out, nand_4_out, nand_5_out, nand_6_out, nand_7_out, nand_8_out,
       nand_9_out, nand_10_out, nand_11_out, nand_12_out, nand_13_out, nand_14_out, nand_15_out, nand_16_out,
       nand_17_out, nand_18_out, nand_19_out, nand_20_out, nand_21_out, nand_22_out, nand_23_out,
       nand_24_out, nand_25_out, nand_26_out, nand_27_out, nand_28_out, nand_29_out, nand_30_out,
       nand_31_out, nand_32_out, nand_33_out, nand_34_out, nand_35_out, nand_36_out, nand_37_out,
       nand_38_out, nand_39_out, nand_40_out, nand_41_out, nand_42_out, nand_43_out, nand_44_out,
       nand_45_out, nand_46_out, nand_47_out, nand_48_out, nand_50_out, nand_51_out, nand_52_out,
       nand_53_out, nand_54_out, nand_55_out, nand_56_out, nand_57_out, nand_58_out, nand_59_out,
       nand_60_out, nand_61_out, nand_62_out, nand_64_out, nor_1_out, not_1_out, not_2_out, not_3_out,
       not_4_out, not_5_out, not_6_out, not_7_out, not_8_out, not_9_out, not_10_out, not_11_out, not_12_out,
       not_13_out, not_14_out, not_15_out, not_16_out, not_17_out, not_18_out, not_19_out, or_1_out,
       or_2_out, or_3_out, or_4_out, or_5_out, or_6_out, or_7_out, or_8_out;

  not not_1 (not_1_out, S1);
  not not_2 (not_2_out, S0);
  and and_1 (and_1_out, SR, not_1_out, S0);
  and and_2 (and_2_out, not_2_out, S1, nand_51_out);
  and and_3 (and_3_out, not_2_out, not_1_out, A);
  and and_4 (and_4_out, S0, S1, QA_prime);
  and and_5 (and_5_out, QA_prime, not_1_out, S0);
  and and_6 (and_6_out, not_2_out, S1, nand_53_out);
  and and_7 (and_7_out, not_2_out, not_1_out, B);
  and and_8 (and_8_out, S0, S1, nand_51_out);
  and and_9 (and_9_out, nand_51_out, not_1_out, S0);
  and and_10 (and_10_out, not_2_out, S1, nand_55_out);
  and and_11 (and_11_out, not_2_out, not_1_out, C);
  and and_12 (and_12_out, S0, S1, nand_53_out);
  and and_13 (and_13_out, nand_53_out, not_1_out, S0);
  and and_14 (and_14_out, not_2_out, S1, nand_57_out);
  and and_15 (and_15_out, not_2_out, not_1_out, D);
  and and_16 (and_16_out, S0, S1, nand_55_out);
  and and_17 (and_17_out, nand_55_out, not_1_out, S0);
  and and_18 (and_18_out, not_2_out, S1, nand_59_out);
  and and_19 (and_19_out, not_2_out, not_1_out, E);
  and and_20 (and_20_out, S0, S1, nand_57_out);
  and and_21 (and_21_out, nand_57_out, not_1_out, S0);
  and and_22 (and_22_out, not_2_out, S1, nand_61_out);
  and and_23 (and_23_out, not_2_out, not_1_out, F);
  and and_24 (and_24_out, S0, S1, nand_59_out);
  and and_25 (and_25_out, nand_59_out, not_1_out, S0);
  and and_26 (and_26_out, not_2_out, S1, QH_prime);
  and and_27 (and_27_out, not_2_out, not_1_out, G);
  and and_28 (and_28_out, S0, S1, nand_61_out);
  and and_29 (and_29_out, nand_61_out, not_1_out, S0);
  and and_30 (and_30_out, not_2_out, S1, SL);
  and and_31 (and_31_out, not_2_out, not_1_out, H);
  and and_32 (and_32_out, S0, S1, QH_prime);
  not not_3 (not_3_out, CLK);
  or or_1 (or_1_out, and_1_out, and_2_out, and_3_out, and_4_out);
  or or_2 (or_2_out, and_5_out, and_6_out, and_7_out, and_8_out);
  or or_3 (or_3_out, and_9_out, and_10_out, and_11_out, and_12_out);
  or or_4 (or_4_out, and_13_out, and_14_out, and_15_out, and_16_out);
  or or_5 (or_5_out, and_17_out, and_18_out, and_19_out, and_20_out);
  or or_6 (or_6_out, and_21_out, and_22_out, and_23_out, and_24_out);
  or or_7 (or_7_out, and_25_out, and_26_out, and_27_out, and_28_out);
  or or_8 (or_8_out, and_29_out, and_30_out, and_31_out, and_32_out);
  and and_33 (and_33_out, S0, S1);
  not not_4 (not_4_out, not_3_out);
  not not_5 (not_5_out, not_3_out);
  not not_6 (not_6_out, not_3_out);
  not not_7 (not_7_out, not_3_out);
  not not_8 (not_8_out, not_3_out);
  not not_9 (not_9_out, not_3_out);
  not not_10 (not_10_out, not_3_out);
  not not_11 (not_11_out, not_3_out);
  nand nand_1 (nand_1_out, or_1_out, not_4_out);
  nand nand_2 (nand_2_out, nand_1_out, not_4_out);
  nand nand_3 (nand_3_out, or_2_out, not_5_out);
  nand nand_4 (nand_4_out, nand_3_out, not_5_out);
  nand nand_5 (nand_5_out, or_3_out, not_6_out);
  nand nand_6 (nand_6_out, nand_5_out, not_6_out);
  nand nand_7 (nand_7_out, or_4_out, not_7_out);
  nand nand_8 (nand_8_out, nand_7_out, not_7_out);
  nand nand_9 (nand_9_out, or_5_out, not_8_out);
  nand nand_10 (nand_10_out, nand_9_out, not_8_out);
  nand nand_11 (nand_11_out, or_6_out, not_9_out);
  nand nand_12 (nand_12_out, nand_11_out, not_9_out);
  nand nand_13 (nand_13_out, or_7_out, not_10_out);
  nand nand_14 (nand_14_out, nand_13_out, not_10_out);
  nand nand_15 (nand_15_out, or_8_out, not_11_out);
  nand nand_16 (nand_16_out, nand_15_out, not_11_out);
  nor nor_1 (nor_1_out, G0, G1, and_33_out);
  nand nand_17 (nand_17_out, nand_1_out, nand_18_out);
  nand nand_18 (nand_18_out, nand_17_out, nand_2_out);
  not not_12 (not_12_out, not_4_out);
  nand nand_19 (nand_19_out, nand_3_out, nand_20_out);
  nand nand_20 (nand_20_out, nand_19_out, nand_4_out);
  not not_13 (not_13_out, not_5_out);
  nand nand_21 (nand_21_out, nand_5_out, nand_22_out);
  nand nand_22 (nand_22_out, nand_21_out, nand_6_out);
  not not_14 (not_14_out, not_6_out);
  nand nand_23 (nand_23_out, nand_7_out, nand_24_out);
  nand nand_24 (nand_24_out, nand_23_out, nand_8_out);
  not not_15 (not_15_out, not_7_out);
  nand nand_25 (nand_25_out, nand_9_out, nand_26_out);
  nand nand_26 (nand_26_out, nand_25_out, nand_10_out);
  not not_16 (not_16_out, not_8_out);
  nand nand_27 (nand_27_out, nand_11_out, nand_28_out);
  nand nand_28 (nand_28_out, nand_27_out, nand_12_out);
  not not_17 (not_17_out, not_9_out);
  nand nand_29 (nand_29_out, nand_13_out, nand_30_out);
  nand nand_30 (nand_30_out, nand_29_out, nand_14_out);
  not not_18 (not_18_out, not_10_out);
  nand nand_31 (nand_31_out, nand_15_out, nand_32_out);
  nand nand_32 (nand_32_out, nand_31_out, nand_16_out);
  not not_19 (not_19_out, not_11_out);
  nand nand_33 (nand_33_out, nand_17_out, not_12_out);
  nand nand_34 (nand_34_out, nand_33_out, not_12_out);
  nand nand_35 (nand_35_out, nand_19_out, not_13_out);
  nand nand_36 (nand_36_out, nand_35_out, not_13_out);
  nand nand_37 (nand_37_out, nand_21_out, not_14_out);
  nand nand_38 (nand_38_out, nand_37_out, not_14_out);
  nand nand_39 (nand_39_out, nand_23_out, not_15_out);
  nand nand_40 (nand_40_out, nand_39_out, not_15_out);
  nand nand_41 (nand_41_out, nand_25_out, not_16_out);
  nand nand_42 (nand_42_out, nand_41_out, not_16_out);
  nand nand_43 (nand_43_out, nand_27_out, not_17_out);
  nand nand_44 (nand_44_out, nand_43_out, not_17_out);
  nand nand_45 (nand_45_out, nand_29_out, not_18_out);
  nand nand_46 (nand_46_out, nand_45_out, not_18_out);
  nand nand_47 (nand_47_out, nand_31_out, not_19_out);
  nand nand_48 (nand_48_out, nand_47_out, not_19_out);
  nand nand_49 (QA_prime, nand_33_out, nand_50_out);
  nand nand_50 (nand_50_out, QA_prime, nand_34_out);
  nand nand_51 (nand_51_out, nand_35_out, nand_52_out);
  nand nand_52 (nand_52_out, nand_51_out, nand_36_out);
  nand nand_53 (nand_53_out, nand_37_out, nand_54_out);
  nand nand_54 (nand_54_out, nand_53_out, nand_38_out);
  nand nand_55 (nand_55_out, nand_39_out, nand_56_out);
  nand nand_56 (nand_56_out, nand_55_out, nand_40_out);
  nand nand_57 (nand_57_out, nand_41_out, nand_58_out);
  nand nand_58 (nand_58_out, nand_57_out, nand_42_out);
  nand nand_59 (nand_59_out, nand_43_out, nand_60_out);
  nand nand_60 (nand_60_out, nand_59_out, nand_44_out);
  nand nand_61 (nand_61_out, nand_45_out, nand_62_out);
  nand nand_62 (nand_62_out, nand_61_out, nand_46_out);
  nand nand_63 (QH_prime, nand_47_out, nand_64_out);
  nand nand_64 (nand_64_out, QH_prime, nand_48_out);
  assign QA = nor_1_out ? QA_prime : 1'bz;  // Controlled_Buffer controlled_buffer_1
  assign QB = nor_1_out ? nand_51_out : 1'bz;  // Controlled_Buffer controlled_buffer_2
  assign QC = nor_1_out ? nand_53_out : 1'bz;  // Controlled_Buffer controlled_buffer_3
  assign QD = nor_1_out ? nand_55_out : 1'bz;  // Controlled_Buffer controlled_buffer_4
  assign QE = nor_1_out ? nand_57_out : 1'bz;  // Controlled_Buffer controlled_buffer_5
  assign QF = nor_1_out ? nand_59_out : 1'bz;  // Controlled_Buffer controlled_buffer_6
  assign QG = nor_1_out ? nand_61_out : 1'bz;  // Controlled_Buffer controlled_buffer_7
  assign QH = nor_1_out ? QH_prime : 1'bz;  // Controlled_Buffer controlled_buffer_8
endmodule
