// Logisim project tests.circ as structural Verilog
module Test_7400 (
);

  wire dip_7400_1_y1, dip_7400_1_y2, dip_7400_1_y3, dip_7400_1_y4, Start_out, tip2_1_p2, tip2_1_p3,
       tip2_1_p5, tip2_1_p6, toc4_1_p8;
  wire [1:0] tip2_1_p4;
  wire [3:0] rom_1_data;

  Button Start (.out(Start_out));
  // TIP2 tip2_1: pin names not known; wires that end beside it: Start_out, tip2_1_p2, tip2_1_p3, tip2_1_p4, tip2_1_p5, tip2_1_p6
  DIP_7400 dip_7400_1 (
    .A1(tip2_1_p5), .B1(tip2_1_p6), .A2(tip2_1_p5), .B2(tip2_1_p6), .A3(tip2_1_p5), .B3(tip2_1_p6),
    .A4(tip2_1_p5), .B4(tip2_1_p6), .Y1(dip_7400_1_y1), .Y2(dip_7400_1_y2), .Y3(dip_7400_1_y3),
    .Y4(dip_7400_1_y4));
  ROM #(.addrWidth(2), .dataWidth(4)) rom_1 (.addr(tip2_1_p4), .data(rom_1_data));  // open: sel
  // TOC4 toc4_1: pin names not known; wires that end beside it: dip_7400_1_y1, dip_7400_1_y2, dip_7400_1_y3, dip_7400_1_y4, rom_1_data, tip2_1_p3, tip2_1_p2, toc4_1_p8
  LED Failure (.in(tip2_1_p2));
  LED Success (.in(toc4_1_p8));

  // Notes on the sheet:
  //   contents of rom_1 (hex, n*v repeats v):
  //   f f f
endmodule

module Test_7402 (
);

  wire dip_7402_1_y1, dip_7402_1_y2, dip_7402_1_y3, dip_7402_1_y4, Start_out, tip2_1_p2, tip2_1_p3,
       tip2_1_p5, tip2_1_p6, toc4_1_p8;
  wire [1:0] tip2_1_p4;
  wire [3:0] rom_1_data;

  Button Start (.out(Start_out));
  // TIP2 tip2_1: pin names not known; wires that end beside it: Start_out, tip2_1_p2, tip2_1_p3, tip2_1_p4, tip2_1_p5, tip2_1_p6
  DIP_7402 dip_7402_1 (
    .A1(tip2_1_p5), .B1(tip2_1_p6), .A2(tip2_1_p5), .B2(tip2_1_p6), .A3(tip2_1_p5), .B3(tip2_1_p6),
    .A4(tip2_1_p5), .B4(tip2_1_p6), .Y1(dip_7402_1_y1), .Y2(dip_7402_1_y2), .Y3(dip_7402_1_y3),
    .Y4(dip_7402_1_y4));
  ROM #(.addrWidth(2), .dataWidth(4)) rom_1 (.addr(tip2_1_p4), .data(rom_1_data));  // open: sel
  // TOC4 toc4_1: pin names not known; wires that end beside it: dip_7402_1_y1, dip_7402_1_y2, dip_7402_1_y3, dip_7402_1_y4, rom_1_data, tip2_1_p3, tip2_1_p2, toc4_1_p8
  LED Failure (.in(tip2_1_p2));
  LED Success (.in(toc4_1_p8));

  // Notes on the sheet:
  //   contents of rom_1 (hex, n*v repeats v):
  //   f
endmodule

module Test_7404 (
);

  wire dip_7404_1_y1, dip_7404_1_y2, dip_7404_1_y3, dip_7404_1_y4, dip_7404_1_y5, dip_7404_1_y6, Start_out,
       tip1_1_p2, tip1_1_p3, tip1_1_p4, tip1_1_p5, toc6_1_p10;
  wire [5:5] not_1_out;

  Button Start (.out(Start_out));
  // TIP1 tip1_1: pin names not known; wires that end beside it: Start_out, tip1_1_p2, tip1_1_p3, tip1_1_p4, tip1_1_p5
  not not_1 (not_1_out[5], tip1_1_p4);
  DIP_7404 dip_7404_1 (
    .A1(tip1_1_p5), .A2(tip1_1_p5), .A3(tip1_1_p5), .A4(tip1_1_p5), .A5(tip1_1_p5), .A6(tip1_1_p5),
    .Y1(dip_7404_1_y1), .Y2(dip_7404_1_y2), .Y3(dip_7404_1_y3), .Y4(dip_7404_1_y4), .Y5(dip_7404_1_y5),
    .Y6(dip_7404_1_y6));
  // TOC6 toc6_1: pin names not known; wires that end beside it: dip_7404_1_y3, dip_7404_1_y2, dip_7404_1_y1, dip_7404_1_y6, dip_7404_1_y5, dip_7404_1_y4, {6{not_1_out[5]}}, tip1_1_p3, tip1_1_p2, toc6_1_p10
  LED Failure (.in(tip1_1_p2));
  LED Success (.in(toc6_1_p10));
endmodule

module Test_7408 (
);

  wire dip_7408_1_y1, dip_7408_1_y2, dip_7408_1_y3, dip_7408_1_y4, Start_out, tip2_1_p2, tip2_1_p3,
       tip2_1_p5, tip2_1_p6, toc4_1_p8;
  wire [1:0] tip2_1_p4;
  wire [3:0] rom_1_data;

  Button Start (.out(Start_out));
  // TIP2 tip2_1: pin names not known; wires that end beside it: Start_out, tip2_1_p2, tip2_1_p3, tip2_1_p4, tip2_1_p5, tip2_1_p6
  DIP_7408 dip_7408_1 (
    .A1(tip2_1_p5), .B1(tip2_1_p6), .A2(tip2_1_p5), .B2(tip2_1_p6), .A3(tip2_1_p5), .B3(tip2_1_p6),
    .A4(tip2_1_p5), .B4(tip2_1_p6), .Y1(dip_7408_1_y1), .Y2(dip_7408_1_y2), .Y3(dip_7408_1_y3),
    .Y4(dip_7408_1_y4));
  ROM #(.addrWidth(2), .dataWidth(4)) rom_1 (.addr(tip2_1_p4), .data(rom_1_data));  // open: sel
  // TOC4 toc4_1: pin names not known; wires that end beside it: dip_7408_1_y1, dip_7408_1_y2, dip_7408_1_y3, dip_7408_1_y4, rom_1_data, tip2_1_p3, tip2_1_p2, toc4_1_p8
  LED Failure (.in(tip2_1_p2));
  LED Success (.in(toc4_1_p8));

  // Notes on the sheet:
  //   contents of rom_1 (hex, n*v repeats v):
  //   0 0 0 f
endmodule

module Test_7410 (
);

  wire dip_7410_1_y1, dip_7410_1_y2, dip_7410_1_y3, Start_out, tip3_1_p2, tip3_1_p3, tip3_1_p5, tip3_1_p6,
       tip3_1_p7, toc3_1_p7;
  wire [2:0] rom_1_data, tip3_1_p4;

  Button Start (.out(Start_out));
  // TIP3 tip3_1: pin names not known; wires that end beside it: Start_out, tip3_1_p2, tip3_1_p3, tip3_1_p4, tip3_1_p5, tip3_1_p6, tip3_1_p7
  DIP_7410 dip_7410_1 (
    .A1(tip3_1_p5), .B1(tip3_1_p6), .C1(tip3_1_p7), .A2(tip3_1_p5), .B2(tip3_1_p6), .C2(tip3_1_p7),
    .A3(tip3_1_p5), .B3(tip3_1_p6), .C3(tip3_1_p7), .Y1(dip_7410_1_y1), .Y2(dip_7410_1_y2), .Y3(dip_7410_1_y3));
  ROM #(.addrWidth(3), .dataWidth(3)) rom_1 (.addr(tip3_1_p4), .data(rom_1_data));  // open: sel
  // TOC3 toc3_1: pin names not known; wires that end beside it: dip_7410_1_y1, dip_7410_1_y2, dip_7410_1_y3, rom_1_data, tip3_1_p3, tip3_1_p2, toc3_1_p7
  LED Failure (.in(tip3_1_p2));
  LED Success (.in(toc3_1_p7));

  // Notes on the sheet:
  //   contents of rom_1 (hex, n*v repeats v):
  //   7*7
endmodule

module Test_7411 (
);

  wire dip_7411_1_y1, dip_7411_1_y2, dip_7411_1_y3, Start_out, tip3_1_p2, tip3_1_p3, tip3_1_p5, tip3_1_p6,
       tip3_1_p7, toc3_1_p7;
  wire [2:0] rom_1_data, tip3_1_p4;

  Button Start (.out(Start_out));
  // TIP3 tip3_1: pin names not known; wires that end beside it: Start_out, tip3_1_p2, tip3_1_p3, tip3_1_p4, tip3_1_p5, tip3_1_p6, tip3_1_p7
  DIP_7411 dip_7411_1 (
    .A1(tip3_1_p5), .B1(tip3_1_p6), .C1(tip3_1_p7), .A2(tip3_1_p5), .B2(tip3_1_p6), .C2(tip3_1_p7),
    .A3(tip3_1_p5), .B3(tip3_1_p6), .C3(tip3_1_p7), .Y1(dip_7411_1_y1), .Y2(dip_7411_1_y2), .Y3(dip_7411_1_y3));
  ROM #(.addrWidth(3), .dataWidth(3)) rom_1 (.addr(tip3_1_p4), .data(rom_1_data));  // open: sel
  // TOC3 toc3_1: pin names not known; wires that end beside it: dip_7411_1_y1, dip_7411_1_y2, dip_7411_1_y3, rom_1_data, tip3_1_p3, tip3_1_p2, toc3_1_p7
  LED Failure (.in(tip3_1_p2));
  LED Success (.in(toc3_1_p7));

  // Notes on the sheet:
  //   contents of rom_1 (hex, n*v repeats v):
  //   7*0 7
endmodule

module Test_7413 (
);

  wire dip_7413_1_y1, dip_7413_1_y2, Start_out, tip4_1_p2, tip4_1_p3, tip4_1_p5, tip4_1_p6, tip4_1_p7,
       tip4_1_p8, toc2_1_p6;
  wire [1:0] rom_1_data;
  wire [3:0] tip4_1_p4;

  Button Start (.out(Start_out));
  // TIP4 tip4_1: pin names not known; wires that end beside it: Start_out, tip4_1_p2, tip4_1_p3, tip4_1_p4, tip4_1_p5, tip4_1_p6, tip4_1_p7, tip4_1_p8
  DIP_7413 dip_7413_1 (
    .A1(tip4_1_p5), .B1(tip4_1_p6), .C1(tip4_1_p7), .D1(tip4_1_p8), .A2(tip4_1_p8), .B2(tip4_1_p7),
    .C2(tip4_1_p6), .D2(tip4_1_p5), .Y1(dip_7413_1_y1), .Y2(dip_7413_1_y2));
  ROM #(.addrWidth(4), .dataWidth(2)) rom_1 (.addr(tip4_1_p4), .data(rom_1_data));  // open: sel
  // TOC2 toc2_1: pin names not known; wires that end beside it: dip_7413_1_y1, dip_7413_1_y2, rom_1_data, tip4_1_p3, tip4_1_p2, toc2_1_p6
  LED Failure (.in(tip4_1_p2));
  LED Success (.in(toc2_1_p6));

  // Notes on the sheet:
  //   contents of rom_1 (hex, n*v repeats v):
  //   15*3
endmodule

module Test_7414 (
);

  wire dip_7414_1_y1, dip_7414_1_y2, dip_7414_1_y3, dip_7414_1_y4, dip_7414_1_y5, dip_7414_1_y6, Start_out,
       tip1_1_p2, tip1_1_p3, tip1_1_p4, tip1_1_p5, toc6_1_p10;
  wire [5:5] not_1_out;

  Button Start (.out(Start_out));
  // TIP1 tip1_1: pin names not known; wires that end beside it: Start_out, tip1_1_p2, tip1_1_p3, tip1_1_p4, tip1_1_p5
  not not_1 (not_1_out[5], tip1_1_p4);
  DIP_7414 dip_7414_1 (
    .A1(tip1_1_p5), .A2(tip1_1_p5), .A3(tip1_1_p5), .A4(tip1_1_p5), .A5(tip1_1_p5), .A6(tip1_1_p5),
    .Y1(dip_7414_1_y1), .Y2(dip_7414_1_y2), .Y3(dip_7414_1_y3), .Y4(dip_7414_1_y4), .Y5(dip_7414_1_y5),
    .Y6(dip_7414_1_y6));
  // TOC6 toc6_1: pin names not known; wires that end beside it: dip_7414_1_y3, dip_7414_1_y2, dip_7414_1_y1, dip_7414_1_y6, dip_7414_1_y5, dip_7414_1_y4, {6{not_1_out[5]}}, tip1_1_p3, tip1_1_p2, toc6_1_p10
  LED Failure (.in(tip1_1_p2));
  LED Success (.in(toc6_1_p10));
endmodule

module Test_7420 (
);

  wire dip_7420_1_y1, dip_7420_1_y2, Start_out, tip4_1_p2, tip4_1_p3, tip4_1_p5, tip4_1_p6, tip4_1_p7,
       tip4_1_p8, toc2_1_p6;
  wire [1:0] rom_1_data;
  wire [3:0] tip4_1_p4;

  Button Start (.out(Start_out));
  // TIP4 tip4_1: pin names not known; wires that end beside it: Start_out, tip4_1_p2, tip4_1_p3, tip4_1_p4, tip4_1_p5, tip4_1_p6, tip4_1_p7, tip4_1_p8
  DIP_7420 dip_7420_1 (
    .A1(tip4_1_p5), .B1(tip4_1_p6), .C1(tip4_1_p7), .D1(tip4_1_p8), .A2(tip4_1_p5), .B2(tip4_1_p6),
    .C2(tip4_1_p7), .D2(tip4_1_p8), .Y1(dip_7420_1_y1), .Y2(dip_7420_1_y2));
  ROM #(.addrWidth(4), .dataWidth(2)) rom_1 (.addr(tip4_1_p4), .data(rom_1_data));  // open: sel
  // TOC2 toc2_1: pin names not known; wires that end beside it: dip_7420_1_y1, dip_7420_1_y2, rom_1_data, tip4_1_p3, tip4_1_p2, toc2_1_p6
  LED Failure (.in(tip4_1_p2));
  LED Success (.in(toc2_1_p6));

  // Notes on the sheet:
  //   contents of rom_1 (hex, n*v repeats v):
  //   15*3
endmodule

module Test_7421 (
);

  wire dip_7421_1_y1, dip_7421_1_y2, Start_out, tip4_1_p2, tip4_1_p3, tip4_1_p5, tip4_1_p6, tip4_1_p7,
       tip4_1_p8, toc2_1_p6;
  wire [1:0] rom_1_data;
  wire [3:0] tip4_1_p4;

  Button Start (.out(Start_out));
  // TIP4 tip4_1: pin names not known; wires that end beside it: Start_out, tip4_1_p2, tip4_1_p3, tip4_1_p4, tip4_1_p5, tip4_1_p6, tip4_1_p7, tip4_1_p8
  DIP_7421 dip_7421_1 (
    .A1(tip4_1_p5), .B1(tip4_1_p6), .C1(tip4_1_p7), .D1(tip4_1_p8), .A2(tip4_1_p5), .B2(tip4_1_p6),
    .C2(tip4_1_p7), .D2(tip4_1_p8), .Y1(dip_7421_1_y1), .Y2(dip_7421_1_y2));
  ROM #(.addrWidth(4), .dataWidth(2)) rom_1 (.addr(tip4_1_p4), .data(rom_1_data));  // open: sel
  // TOC2 toc2_1: pin names not known; wires that end beside it: dip_7421_1_y1, dip_7421_1_y2, rom_1_data, tip4_1_p3, tip4_1_p2, toc2_1_p6
  LED Failure (.in(tip4_1_p2));
  LED Success (.in(toc2_1_p6));

  // Notes on the sheet:
  //   contents of rom_1 (hex, n*v repeats v):
  //   15*0 3
endmodule

module Test_7425 (
);

  wire dip_7425_1_y1, dip_7425_1_y2, Start_out, tip4_1_p2, tip4_1_p3, tip4_1_p5, tip4_1_p6, tip4_1_p7,
       tip4_1_p8, toc2_1_p6;
  wire [1:0] rom_1_data;
  wire [3:0] tip4_1_p4;

  Button Start (.out(Start_out));
  // TIP4 tip4_1: pin names not known; wires that end beside it: Start_out, tip4_1_p2, tip4_1_p3, tip4_1_p4, tip4_1_p5, tip4_1_p6, tip4_1_p7, tip4_1_p8
  DIP_7425 dip_7425_1 (
    .A1(tip4_1_p5), .B1(tip4_1_p6), .C1(tip4_1_p7), .D1(tip4_1_p8), .A2(tip4_1_p5), .B2(tip4_1_p6),
    .C2(tip4_1_p7), .D2(tip4_1_p8), .Y1(dip_7425_1_y1), .Y2(dip_7425_1_y2));
  ROM #(.addrWidth(4), .dataWidth(2)) rom_1 (.addr(tip4_1_p4), .data(rom_1_data));  // open: sel
  // TOC2 toc2_1: pin names not known; wires that end beside it: dip_7425_1_y1, dip_7425_1_y2, rom_1_data, tip4_1_p3, tip4_1_p2, toc2_1_p6
  LED Failure (.in(tip4_1_p2));
  LED Success (.in(toc2_1_p6));

  // Notes on the sheet:
  //   contents of rom_1 (hex, n*v repeats v):
  //   3
endmodule

module Test_7427 (
);

  wire dip_7427_1_y1, dip_7427_1_y2, dip_7427_1_y3, Start_out, tip3_1_p2, tip3_1_p3, tip3_1_p5, tip3_1_p6,
       tip3_1_p7, toc3_1_p7;
  wire [2:0] rom_1_data, tip3_1_p4;

  Button Start (.out(Start_out));
  // TIP3 tip3_1: pin names not known; wires that end beside it: Start_out, tip3_1_p2, tip3_1_p3, tip3_1_p4, tip3_1_p5, tip3_1_p6, tip3_1_p7
  DIP_7427 dip_7427_1 (
    .A1(tip3_1_p5), .B1(tip3_1_p6), .C1(tip3_1_p7), .A2(tip3_1_p5), .B2(tip3_1_p6), .C2(tip3_1_p7),
    .A3(tip3_1_p5), .B3(tip3_1_p6), .C3(tip3_1_p7), .Y1(dip_7427_1_y1), .Y2(dip_7427_1_y2), .Y3(dip_7427_1_y3));
  ROM #(.addrWidth(3), .dataWidth(3)) rom_1 (.addr(tip3_1_p4), .data(rom_1_data));  // open: sel
  // TOC3 toc3_1: pin names not known; wires that end beside it: dip_7427_1_y1, dip_7427_1_y2, dip_7427_1_y3, rom_1_data, tip3_1_p3, tip3_1_p2, toc3_1_p7
  LED Failure (.in(tip3_1_p2));
  LED Success (.in(toc3_1_p7));

  // Notes on the sheet:
  //   contents of rom_1 (hex, n*v repeats v):
  //   7
endmodule

module Test_7430 (
);

  wire dip_7430_1_y, rom_1_data, Start_out, tip8_1_p2, tip8_1_p3, tip8_1_p5, tip8_1_p6, tip8_1_p7, tip8_1_p8,
       tip8_1_p9, tip8_1_p10, tip8_1_p11, tip8_1_p12, toc1_1_p5;
  wire [7:0] tip8_1_p4;

  Button Start (.out(Start_out));
  // TIP8 tip8_1: pin names not known; wires that end beside it: Start_out, tip8_1_p2, tip8_1_p3, tip8_1_p4, tip8_1_p5, tip8_1_p6, tip8_1_p7, tip8_1_p8, tip8_1_p9, tip8_1_p10, tip8_1_p11, tip8_1_p12
  DIP_7430 dip_7430_1 (
    .A(tip8_1_p5), .B(tip8_1_p6), .C(tip8_1_p7), .D(tip8_1_p8), .E(tip8_1_p9), .F(tip8_1_p10),
    .G(tip8_1_p11), .H(tip8_1_p12), .Y(dip_7430_1_y));
  ROM #(.dataWidth(1)) rom_1 (.addr(tip8_1_p4), .data(rom_1_data));  // open: sel
  // TOC1 toc1_1: pin names not known; wires that end beside it: dip_7430_1_y, rom_1_data, tip8_1_p3, tip8_1_p2, toc1_1_p5
  LED Failure (.in(tip8_1_p2));
  LED Success (.in(toc1_1_p5));

  // Notes on the sheet:
  //   contents of rom_1 (hex, n*v repeats v):
  //   255*1
endmodule

module Test_7432 (
);

  wire dip_7432_1_y1, dip_7432_1_y2, dip_7432_1_y3, dip_7432_1_y4, Start_out, tip2_1_p2, tip2_1_p3,
       tip2_1_p5, tip2_1_p6, toc4_1_p8;
  wire [1:0] tip2_1_p4;
  wire [3:0] rom_1_data;

  Button Start (.out(Start_out));
  // TIP2 tip2_1: pin names not known; wires that end beside it: Start_out, tip2_1_p2, tip2_1_p3, tip2_1_p4, tip2_1_p5, tip2_1_p6
  DIP_7432 dip_7432_1 (
    .A1(tip2_1_p5), .B1(tip2_1_p6), .A2(tip2_1_p5), .B2(tip2_1_p6), .A3(tip2_1_p5), .B3(tip2_1_p6),
    .A4(tip2_1_p5), .B4(tip2_1_p6), .Y1(dip_7432_1_y1), .Y2(dip_7432_1_y2), .Y3(dip_7432_1_y3),
    .Y4(dip_7432_1_y4));
  ROM #(.addrWidth(2), .dataWidth(4)) rom_1 (.addr(tip2_1_p4), .data(rom_1_data));  // open: sel
  // TOC4 toc4_1: pin names not known; wires that end beside it: dip_7432_1_y1, dip_7432_1_y2, dip_7432_1_y4, dip_7432_1_y3, rom_1_data, tip2_1_p3, tip2_1_p2, toc4_1_p8
  LED Failure (.in(tip2_1_p2));
  LED Success (.in(toc4_1_p8));

  // Notes on the sheet:
  //   contents of rom_1 (hex, n*v repeats v):
  //   0 f f f
endmodule

module Test_7451 (
);

  wire dip_7451_1_y1, dip_7451_2_y2, rom_1_data, rom_2_data, Start_2_out, Start_out, tip4_1_p2, tip4_1_p3,
       tip4_1_p5, tip4_1_p6, tip4_1_p7, tip4_1_p8, tip6_1_p2, tip6_1_p3, tip6_1_p5, tip6_1_p6, tip6_1_p7,
       tip6_1_p8, tip6_1_p9, tip6_1_p10, toc1_1_p5, toc1_2_p5;
  wire [3:0] tip4_1_p4;
  wire [5:0] tip6_1_p4;

  Button Start (.out(Start_out));
  Button Start_2 (.out(Start_2_out));
  // TIP6 tip6_1: pin names not known; wires that end beside it: Start_out, tip6_1_p2, tip6_1_p3, tip6_1_p4, tip6_1_p5, tip6_1_p6, tip6_1_p7, tip6_1_p8, tip6_1_p9, tip6_1_p10
  // TIP4 tip4_1: pin names not known; wires that end beside it: Start_2_out, tip4_1_p2, tip4_1_p3, tip4_1_p4, tip4_1_p5, tip4_1_p6, tip4_1_p7, tip4_1_p8
  DIP_7451 dip_7451_1 (
    .A1(tip6_1_p5), .B1(tip6_1_p6), .C1(tip6_1_p7), .D1(tip6_1_p8), .E1(tip6_1_p9), .F1(tip6_1_p10),
    .Y1(dip_7451_1_y1));  // open: A2, B2, C2, D2, Y2
  DIP_7451 dip_7451_2 (
    .A2(tip4_1_p5), .B2(tip4_1_p6), .C2(tip4_1_p7), .D2(tip4_1_p8), .Y2(dip_7451_2_y2));  // open: A1, B1, C1, D1, E1, F1, Y1
  ROM #(.addrWidth(6), .dataWidth(1)) rom_1 (.addr(tip6_1_p4), .data(rom_1_data));  // open: sel
  ROM #(.addrWidth(4), .dataWidth(1)) rom_2 (.addr(tip4_1_p4), .data(rom_2_data));  // open: sel
  // TOC1 toc1_1: pin names not known; wires that end beside it: dip_7451_1_y1, rom_1_data, tip6_1_p3, tip6_1_p2, toc1_1_p5
  // TOC1 toc1_2: pin names not known; wires that end beside it: dip_7451_2_y2, rom_2_data, tip4_1_p3, tip4_1_p2, toc1_2_p5
  LED Failure (.in(tip6_1_p2));
  LED Success (.in(toc1_1_p5));
  LED Failure_2 (.in(tip4_1_p2));
  LED Success_2 (.in(toc1_2_p5));

  // Notes on the sheet:
  //   contents of rom_1 (hex, n*v repeats v):
  //   7*1 0 7*1 0 7*1 0 7*1 0 7*1 0 7*1 0 7*1
  //   contents of rom_2 (hex, n*v repeats v):
  //   1 1 1 0 1 1 1 0 1 1 1
endmodule

module Test_7485 (
);

  wire and_1_out, and_2_out, and_3_out, comparator_1_eq, comparator_1_gt, comparator_1_lt, dip_7485_1_yeq,
       dip_7485_1_ygt, dip_7485_1_ylt, not_1_out, not_2_out, not_3_out, Start_out, tip11_1_p2, tip11_1_p3,
       tip11_1_p5, tip11_1_p6, tip11_1_p7, tip11_1_p8, tip11_1_p9, tip11_1_p10, tip11_1_p11, tip11_1_p12,
       tip11_1_p13, tip11_1_p14, tip11_1_p15, toc3_1_p7;
  wire [2:0] or_1_out;
  wire [10:0] tip11_1_p4;

  Button Start (.out(Start_out));
  // TIP11 tip11_1: pin names not known; wires that end beside it: Start_out, tip11_1_p2, tip11_1_p3, tip11_1_p4, tip11_1_p5, tip11_1_p6, tip11_1_p7, tip11_1_p8, tip11_1_p9, tip11_1_p10, tip11_1_p11, tip11_1_p12, tip11_1_p13, tip11_1_p14, tip11_1_p15
  Comparator #(.width(4), .mode("unsigned")) comparator_1 (
    .a(tip11_1_p4[3:0]), .b(tip11_1_p4[7:4]), .gt(comparator_1_gt), .eq(comparator_1_eq), .lt(comparator_1_lt));
  DIP_7485 dip_7485_1 (
    .A4(tip11_1_p8), .B4(tip11_1_p12), .A3(tip11_1_p7), .B3(tip11_1_p11), .CLT(tip11_1_p13),
    .CEQ(tip11_1_p14), .CGT(tip11_1_p15), .A2(tip11_1_p6), .B2(tip11_1_p10), .A1(tip11_1_p5),
    .B1(tip11_1_p9), .YGT(dip_7485_1_ygt), .YEQ(dip_7485_1_yeq), .YLT(dip_7485_1_ylt));
  not not_1 (not_1_out, tip11_1_p4[8]);
  not not_2 (not_2_out, tip11_1_p4[10]);
  not not_3 (not_3_out, tip11_1_p4[9]);
  and and_1 (and_1_out, comparator_1_eq, not_1_out, not_3_out, tip11_1_p4[10]);
  and and_2 (and_2_out, comparator_1_eq, tip11_1_p4[8], not_3_out, not_2_out);
  and and_3 (and_3_out, comparator_1_eq, not_1_out, not_3_out, not_2_out);
  or or_1 (or_1_out[0], and_3_out, and_2_out, comparator_1_lt);
  and and_4 (or_1_out[1], tip11_1_p4[9], comparator_1_eq);
  or or_2 (or_1_out[2], and_3_out, and_1_out, comparator_1_gt);
  // TOC3 toc3_1: pin names not known; wires that end beside it: dip_7485_1_ylt, dip_7485_1_yeq, dip_7485_1_ygt, or_1_out, tip11_1_p3, tip11_1_p2, toc3_1_p7
  LED Failure (.in(tip11_1_p2));
  LED Success (.in(toc3_1_p7));
endmodule

module Test_4786 (
);

  wire dip_7486_1_y1, dip_7486_1_y2, dip_7486_1_y3, dip_7486_1_y4, Start_out, tip2_1_p2, tip2_1_p3,
       tip2_1_p5, tip2_1_p6, toc4_1_p8;
  wire [1:0] tip2_1_p4;
  wire [3:0] rom_1_data;

  Button Start (.out(Start_out));
  // TIP2 tip2_1: pin names not known; wires that end beside it: Start_out, tip2_1_p2, tip2_1_p3, tip2_1_p4, tip2_1_p5, tip2_1_p6
  DIP_7486 dip_7486_1 (
    .A1(tip2_1_p5), .B1(tip2_1_p6), .A2(tip2_1_p5), .B2(tip2_1_p6), .A3(tip2_1_p5), .B3(tip2_1_p6),
    .A4(tip2_1_p5), .B4(tip2_1_p6), .Y1(dip_7486_1_y1), .Y2(dip_7486_1_y2), .Y3(dip_7486_1_y3),
    .Y4(dip_7486_1_y4));
  ROM #(.addrWidth(2), .dataWidth(4)) rom_1 (.addr(tip2_1_p4), .data(rom_1_data));  // open: sel
  // TOC4 toc4_1: pin names not known; wires that end beside it: dip_7486_1_y1, dip_7486_1_y2, dip_7486_1_y4, dip_7486_1_y3, rom_1_data, tip2_1_p3, tip2_1_p2, toc4_1_p8
  LED Failure (.in(tip2_1_p2));
  LED Success (.in(toc4_1_p8));

  // Notes on the sheet:
  //   contents of rom_1 (hex, n*v repeats v):
  //   0 f f
endmodule

module Test_74138 (
);

  wire and_1_out, decoder_1_out0, decoder_1_out1, decoder_1_out2, decoder_1_out3, decoder_1_out4,
       decoder_1_out5, decoder_1_out6, decoder_1_out7, dip_74138_1_y0, dip_74138_1_y1, dip_74138_1_y2,
       dip_74138_1_y3, dip_74138_1_y4, dip_74138_1_y5, dip_74138_1_y6, dip_74138_1_y7, not_1_out, not_2_out,
       Start_out, tip6_1_p2, tip6_1_p3, tip6_1_p5, tip6_1_p6, tip6_1_p7, tip6_1_p8, tip6_1_p9, tip6_1_p10,
       toc8_1_p12;
  wire [5:0] tip6_1_p4;
  wire [7:0] not_10_out;

  Button Start (.out(Start_out));
  // TIP6 tip6_1: pin names not known; wires that end beside it: Start_out, tip6_1_p2, tip6_1_p3, tip6_1_p4, tip6_1_p5, tip6_1_p6, tip6_1_p7, tip6_1_p8, tip6_1_p9, tip6_1_p10
  not not_1 (not_1_out, tip6_1_p4[3]);
  not not_2 (not_2_out, tip6_1_p4[4]);
  DIP_74138 dip_74138_1 (
    .A0(tip6_1_p5), .A1(tip6_1_p6), .A2(tip6_1_p7), .E1(tip6_1_p8), .E2(tip6_1_p9), .E2_2(tip6_1_p10),
    .Y0(dip_74138_1_y0), .Y1(dip_74138_1_y1), .Y2(dip_74138_1_y2), .Y3(dip_74138_1_y3), .Y4(dip_74138_1_y4),
    .Y5(dip_74138_1_y5), .Y6(dip_74138_1_y6), .Y7(dip_74138_1_y7));
  Decoder #(.select(3), .disabled(0)) decoder_1 (
    .out0(decoder_1_out0), .out1(decoder_1_out1), .out2(decoder_1_out2), .out3(decoder_1_out3),
    .out4(decoder_1_out4), .out5(decoder_1_out5), .out6(decoder_1_out6), .out7(decoder_1_out7),
    .sel(tip6_1_p4[2:0]), .en(and_1_out));
  and and_1 (and_1_out, not_1_out, not_2_out, tip6_1_p4[5]);
  not not_3 (not_10_out[5], decoder_1_out5);
  not not_4 (not_10_out[7], decoder_1_out7);
  not not_5 (not_10_out[6], decoder_1_out6);
  not not_6 (not_10_out[4], decoder_1_out4);
  not not_7 (not_10_out[3], decoder_1_out3);
  not not_8 (not_10_out[2], decoder_1_out2);
  not not_9 (not_10_out[1], decoder_1_out1);
  not not_10 (not_10_out[0], decoder_1_out0);
  // TOC8 toc8_1: pin names not known; wires that end beside it: dip_74138_1_y0, dip_74138_1_y1, dip_74138_1_y2, dip_74138_1_y3, dip_74138_1_y4, dip_74138_1_y5, dip_74138_1_y6, dip_74138_1_y7, not_10_out, tip6_1_p3, tip6_1_p2, toc8_1_p12
  LED Failure (.in(tip6_1_p2));
  LED Success (.in(toc8_1_p12));
endmodule

module Test_74238_TODO (
);

  wire and_1_out, dip_74238_1_p7, dip_74238_1_p8, dip_74238_1_p9, dip_74238_1_p10, dip_74238_1_p11,
       dip_74238_1_p12, dip_74238_1_p13, dip_74238_1_p14, not_1_out, not_2_out, Start_out, tip6_1_p2,
       tip6_1_p3, tip6_1_p5, tip6_1_p6, tip6_1_p7, tip6_1_p8, tip6_1_p9, tip6_1_p10, toc8_1_p12;
  wire [5:0] tip6_1_p4;
  wire [7:0] decoder_1_out0;

  Button Start (.out(Start_out));
  // TIP6 tip6_1: pin names not known; wires that end beside it: Start_out, tip6_1_p2, tip6_1_p3, tip6_1_p4, tip6_1_p5, tip6_1_p6, tip6_1_p7, tip6_1_p8, tip6_1_p9, tip6_1_p10
  not not_1 (not_1_out, tip6_1_p4[3]);
  not not_2 (not_2_out, tip6_1_p4[4]);
  // DIP_74238 dip_74238_1: pin names not known; wires that end beside it: tip6_1_p5, tip6_1_p6, tip6_1_p7, tip6_1_p8, tip6_1_p9, tip6_1_p10, dip_74238_1_p7, dip_74238_1_p8, dip_74238_1_p9, dip_74238_1_p10, dip_74238_1_p11, dip_74238_1_p12, dip_74238_1_p13, dip_74238_1_p14
  Decoder #(.select(3), .disabled(0)) decoder_1 (
    .out0(decoder_1_out0[0]), .out1(decoder_1_out0[1]), .out2(decoder_1_out0[2]), .out3(decoder_1_out0[3]),
    .out4(decoder_1_out0[4]), .out5(decoder_1_out0[5]), .out6(decoder_1_out0[6]), .out7(decoder_1_out0[7]),
    .sel(tip6_1_p4[2:0]), .en(and_1_out));
  and and_1 (and_1_out, not_1_out, not_2_out, tip6_1_p4[5]);
  // TOC8 toc8_1: pin names not known; wires that end beside it: dip_74238_1_p8, dip_74238_1_p9, dip_74238_1_p10, dip_74238_1_p11, dip_74238_1_p12, dip_74238_1_p13, dip_74238_1_p14, dip_74238_1_p7, decoder_1_out0, tip6_1_p3, tip6_1_p2, toc8_1_p12
  LED Failure (.in(tip6_1_p2));
  LED Success (.in(toc8_1_p12));
endmodule

module Test_74283 (
);

  wire dip_74283_1_cout, dip_74283_1_y1, dip_74283_1_y2, dip_74283_1_y3, dip_74283_1_y4, Start_out,
       tip9_1_p2, tip9_1_p3, tip9_1_p5, tip9_1_p6, tip9_1_p7, tip9_1_p8, tip9_1_p9, tip9_1_p10, tip9_1_p11,
       tip9_1_p12, tip9_1_p13, toc5_1_p9;
  wire [3:0] adder_1_out;
  wire [4:4] adder_1_cout;
  wire [8:0] tip9_1_p4;

  Button Start (.out(Start_out));
  // TIP9 tip9_1: pin names not known; wires that end beside it: Start_out, tip9_1_p2, tip9_1_p3, tip9_1_p4, tip9_1_p5, tip9_1_p6, tip9_1_p7, tip9_1_p8, tip9_1_p9, tip9_1_p10, tip9_1_p11, tip9_1_p12, tip9_1_p13
  Adder #(.width(4)) adder_1 (
    .a(tip9_1_p4[3:0]), .b(tip9_1_p4[7:4]), .out(adder_1_out), .cin(tip9_1_p4[8]), .cout(adder_1_cout[4]));
  DIP_74283 dip_74283_1 (
    .CIN(tip9_1_p13), .A1(tip9_1_p5), .B1(tip9_1_p9), .A2(tip9_1_p6), .B2(tip9_1_p10), .A3(tip9_1_p7),
    .B3(tip9_1_p11), .A4(tip9_1_p8), .B4(tip9_1_p12), .Y1(dip_74283_1_y1), .Y2(dip_74283_1_y2),
    .Y3(dip_74283_1_y3), .Y4(dip_74283_1_y4), .COUT(dip_74283_1_cout));
  // TOC5 toc5_1: pin names not known; wires that end beside it: dip_74283_1_y1, dip_74283_1_y2, dip_74283_1_y3, dip_74283_1_y4, dip_74283_1_cout, {adder_1_cout[4], adder_1_out}, tip9_1_p3, tip9_1_p2, toc5_1_p9
  LED Failure (.in(tip9_1_p2));
  LED Success (.in(toc5_1_p9));
endmodule

module Test_744075 (
);

  wire dip_744075_1_y1, dip_744075_1_y2, dip_744075_1_y3, Start_out, tip3_1_p2, tip3_1_p3, tip3_1_p5,
       tip3_1_p6, tip3_1_p7, toc3_1_p7;
  wire [2:0] rom_1_data, tip3_1_p4;

  Button Start (.out(Start_out));
  // TIP3 tip3_1: pin names not known; wires that end beside it: Start_out, tip3_1_p2, tip3_1_p3, tip3_1_p4, tip3_1_p5, tip3_1_p6, tip3_1_p7
  DIP_744075 dip_744075_1 (
    .A1(tip3_1_p5), .B1(tip3_1_p6), .C1(tip3_1_p7), .A2(tip3_1_p5), .B2(tip3_1_p6), .C2(tip3_1_p7),
    .A3(tip3_1_p5), .B3(tip3_1_p6), .C3(tip3_1_p7), .Y1(dip_744075_1_y1), .Y2(dip_744075_1_y2),
    .Y3(dip_744075_1_y3));
  ROM #(.addrWidth(3), .dataWidth(3)) rom_1 (.addr(tip3_1_p4), .data(rom_1_data));  // open: sel
  // TOC3 toc3_1: pin names not known; wires that end beside it: dip_744075_1_y1, dip_744075_1_y2, dip_744075_1_y3, rom_1_data, tip3_1_p3, tip3_1_p2, toc3_1_p7
  LED Failure (.in(tip3_1_p2));
  LED Success (.in(toc3_1_p7));

  // Notes on the sheet:
  //   contents of rom_1 (hex, n*v repeats v):
  //   0 7*7
endmodule

module Test_744511 (
);

  wire dip_744511_1_ya, dip_744511_1_yb, dip_744511_1_yc, dip_744511_1_yd, dip_744511_1_ye, dip_744511_1_yf,
       dip_744511_1_yg, Start_out, tip7_1_p2, tip7_1_p3, tip7_1_p5, tip7_1_p6, tip7_1_p7, tip7_1_p8,
       tip7_1_p9, tip7_1_p10, tip7_1_p11, toc7_1_p11;
  wire [6:0] rom_1_data, tip7_1_p4;

  Button Start (.out(Start_out));
  // TIP7 tip7_1: pin names not known; wires that end beside it: Start_out, tip7_1_p2, tip7_1_p3, tip7_1_p4, tip7_1_p5, tip7_1_p6, tip7_1_p7, tip7_1_p8, tip7_1_p9, tip7_1_p10, tip7_1_p11
  DIP_744511 dip_744511_1 (
    .LT(tip7_1_p9), .D1(tip7_1_p5), .D2(tip7_1_p6), .D3(tip7_1_p7), .D4(tip7_1_p8), .LE(tip7_1_p11),
    .BL(tip7_1_p10), .Ya(dip_744511_1_ya), .Yb(dip_744511_1_yb), .Yc(dip_744511_1_yc), .Yd(dip_744511_1_yd),
    .Ye(dip_744511_1_ye), .Yf(dip_744511_1_yf), .Yg(dip_744511_1_yg));
  LED Lamp_Test (.in(tip7_1_p9));
  LED Blank (.in(tip7_1_p10));
  LED Load_Enable (.in(tip7_1_p11));
  ROM #(.addrWidth(7), .dataWidth(7)) rom_1 (.addr(tip7_1_p4), .data(rom_1_data));  // open: sel
  // TOC7 toc7_1: pin names not known; wires that end beside it: dip_744511_1_ya, dip_744511_1_yb, dip_744511_1_yc, dip_744511_1_yd, dip_744511_1_ye, dip_744511_1_yf, dip_744511_1_yg, rom_1_data, tip7_1_p3, tip7_1_p2, toc7_1_p11
  _7_Segment_Display u_7_segment_display_1 (
    .g(dip_744511_1_yg), .f(dip_744511_1_yf), .a(dip_744511_1_ya), .b(dip_744511_1_yb), .e(dip_744511_1_ye),
    .d(dip_744511_1_yd), .c(dip_744511_1_yc));  // open: dp
  LED Failure (.in(tip7_1_p2));
  LED Success (.in(toc7_1_p11));

  // Notes on the sheet:
  //   contents of rom_1 (hex, n*v repeats v):
  //   16*7f 16*0 16*7f 16*3f 16*7f 16*0 16*7f 3f 6
endmodule
